// Digital circuit 01.dig as structural Verilog
module _01 (
  input  reset,
  input  clk,
  output A,
  output B,
  output C
);

  wire A_t, and_1_out, and_2_out, and_3_out, B_t, C_t, DB, DC;

  xor xor_1 (DC, A, C);
  D_FF_AS d_ff_as_1 (.Set(~1'b1), .D(DC), .C(clk), .Clr(reset), .Q(C), .nQ(C_t));
  and and_1 (and_1_out, C_t, B, A);
  and and_2 (and_2_out, C, B_t);
  and and_3 (and_3_out, B_t, A_t);
  D_FF_AS d_ff_as_2 (.Set(~1'b1), .D(DB), .C(clk), .Clr(reset), .Q(B), .nQ(B_t));
  or or_1 (DB, and_1_out, and_2_out, and_3_out);
  D_FF_AS d_ff_as_3 (.Set(~1'b1), .D(A_t), .C(clk), .Clr(reset), .Q(A), .nQ(A_t));

  // Other names for the same wires on the sheet: DA = A_t

  // Notes on the sheet:
  //   reset: default 1
endmodule

/* Test case T1:
clk reset C B A
0 0 0 0 0 
0 1 0 0 0
1 1 0 0 0
0 0 0 0 0
1 0 0 1 1
0 0 0 1 1
1 0 1 1 0
0 0 1 1 0 
1 0 1 0 1
0 0 1 0 1
1 0 0 1 0
0 0 0 1 0
1 0 0 0 1
0 0 0 0 1
1 0 1 0 0
0 0 1 0 0
1 0 1 1 1
0 0 1 1 1
1 0 0 0 0
0 0 0 0 0
1 0 0 1 1
0 0 0 1 1
1 0 1 1 0
0 0 1 1 0 
1 0 1 0 1
0 0 1 0 1
1 0 0 1 0
0 0 0 1 0
1 0 0 0 1
0 0 0 0 1
1 0 1 0 0
0 0 1 0 0
1 0 1 1 1
0 0 1 1 1
*/
