// Digital circuit 02.dig as structural Verilog
module _02 (
  input  [15:0] A,
  input  \input ,
  input  clk,
  input  [3:0] R,
  output [15:0] nroot,
  output busy
);

  wire and_2_out, and_4_out, and_5_out, comparator_1_gt, comparator_1_lt, comparator_3_eq, comparator_4_lt,
       Count, Count_done, d_ff_1_q, d_ff_2_nq, enb_pwr, input_t, Mul_exceed, not_1_out, or_1_out, or_2_out,
       or_3_out, or_4_out, or_5_out, Pwr_done;
  wire [1:0] register_1_q;
  wire [3:0] counter_1_out;
  wire [15:0] add_1_s, add_2_s, barrelshifter_1_out, H, L, Mid, multiplexer_1_out, multiplexer_2_out,
       multiplexer_3_out, Pwr, sub_1_s, sub_2_s;
  wire [31:0] mul_1_mul;

  D_FF d_ff_1 (.D(\input ), .C(clk), .Q(d_ff_1_q));  // open: nQ
  D_FF d_ff_2 (.D(d_ff_1_q), .C(clk), .nQ(d_ff_2_nq));  // open: Q
  Sub #(.Bits(16)) sub_1 (.a(H), .b(L), .c_i(1'b0), .s(sub_1_s));  // open: c_o
  and and_1 (input_t, d_ff_1_q, d_ff_2_nq);
  Comparator #(.Bits(16)) comparator_1 (.a(Pwr), .b(Mid), .gt(comparator_1_gt), .lt(comparator_1_lt));  // open: eq
  or or_1 (or_1_out, input_t, comparator_1_gt);
  or or_2 (or_2_out, comparator_1_lt, input_t);
  or or_3 (or_3_out, input_t, Pwr_done);
  BarrelShifter #(.Bits(16), .barrelShifterMode("arithmetic"), .direction("right")) barrelshifter_1 (
    .in(sub_1_s), .shift(5'b00001), .out(barrelshifter_1_out));
  Register register_1 (.D(or_1_out), .C(clk), .en(or_3_out), .Q(register_1_q[1]));
  Register register_2 (.D(or_2_out), .C(clk), .en(or_3_out), .Q(register_1_q[0]));
  or or_4 (or_4_out, enb_pwr, and_4_out);
  and and_2 (and_2_out, ~busy, input_t);  // And
  Add #(.Bits(16)) add_1 (.a(Mid), .b(16'h1), .c_i(1'b0), .s(add_1_s));  // open: c_o
  Sub #(.Bits(16)) sub_2 (.a(Mid), .b(16'h1), .c_i(1'b0), .s(sub_2_s));  // open: c_o
  Add #(.Bits(16)) add_2 (.a(L), .b(barrelshifter_1_out), .c_i(1'b0), .s(add_2_s));  // open: c_o
  and and_3 (Count, ~Pwr_done, or_4_out);  // And
  Multiplexer #(.Selector_Bits(2), .Bits(16)) multiplexer_1 (
    .sel(register_1_q), .in_0(L), .in_1(add_1_s), .in_2(L), .in_3({16{1'b0}}), .out(multiplexer_1_out));
  Multiplexer #(.Selector_Bits(2), .Bits(16)) multiplexer_2 (
    .sel(register_1_q), .in_0(H), .in_1(H), .in_2(sub_2_s), .in_3(A), .out(multiplexer_2_out));
  Register #(.Bits(16)) u_Mid (.D(add_2_s), .C(clk), .en(not_1_out), .Q(Mid));
  and and_4 (and_4_out, comparator_4_lt, Count);
  Mul #(.Bits(16)) mul_1 (.a(Mid), .b(Pwr), .mul(mul_1_mul));
  T_FF t_ff_1 (.T(and_2_out), .C(clk), .Q(busy));  // open: nQ
  Counter #(.Bits(4)) counter_1 (.en(Count), .C(clk), .clr(enb_pwr), .out(counter_1_out));  // open: ovf
  Register #(.Bits(16)) u_L (.D(multiplexer_1_out), .C(clk), .en(busy), .Q(L));
  Register #(.Bits(16)) u_H (.D(multiplexer_2_out), .C(clk), .en(busy), .Q(H));
  Comparator #(.Bits(16)) comparator_2 (.a(mul_1_mul[31:16]), .b({16{1'b0}}), .gt(Mul_exceed));  // open: eq, lt
  Comparator #(.Bits(16)) comparator_3 (.a(add_2_s), .b(Mid), .eq(comparator_3_eq));  // open: gt, lt
  Comparator #(.Bits(4)) comparator_4 (.a(counter_1_out), .b(R), .eq(Count_done), .lt(comparator_4_lt));  // open: gt
  not not_1 (not_1_out, comparator_3_eq);
  Multiplexer #(.Bits(16)) multiplexer_3 (
    .sel(and_5_out), .in_0(16'h1), .in_1(mul_1_mul[15:0]), .out(multiplexer_3_out));
  and and_5 (and_5_out, ~Count_done, Count);  // And
  D_FF d_ff_3 (.D(not_1_out), .C(clk), .Q(enb_pwr));  // open: nQ
  or or_5 (or_5_out, Count, ~Pwr_done);  // Or
  Register #(.Bits(16)) u_Pwr (.D(multiplexer_3_out), .C(clk), .en(or_5_out), .Q(Pwr));
  or or_6 (Pwr_done, Count_done, Mul_exceed);

  assign nroot = A;
endmodule

/* Test case TestCase1:
clk A R input nroot busy
0 0 0 0 X 0
1 0 0 0 X 0
0 0 0 0 X 0
1 0 0 0 X 0
0 2 2 1 X X
1 2 2 1 X X
repeat (255) C 2 2 0 X X
0 2 2 0 1 0
1 2 2 0 1 0
0 0 0 0 X 0
1 0 0 0 X 0
0 0 0 0 X 0
1 0 0 0 X 0
0 4 2 1 X X
1 4 2 1 X X
repeat (255) C 4 2 0 X X
0 4 2 0 2 0
1 4 2 0 2 0
0 0 0 0 X 0
1 0 0 0 X 0
0 0 0 0 X 0
1 0 0 0 X 0
0 8 2 1 X X
1 8 2 1 X X
repeat (255) C 8 2 0 X X
0 8 2 0 2 0
1 8 2 0 2 0
0 0 0 0 X 0
1 0 0 0 X 0
0 0 0 0 X 0
1 0 0 0 X 0
0 16 2 1 X X
1 16 2 1 X X
repeat (255) C 16 2 0 X X
0 16 2 0 4 0
1 16 2 0 4 0
*/

/* Test case TestCase4:
clk A R input nroot busy
0 0 0 0 X 0
1 0 0 0 X 0
0 0 0 0 X 0
1 0 0 0 X 0
0 65530 12 1 X X
1 65530 12 1 X X
repeat (255) C 65530 12 0 X X
0 65530 12 0 2 0
1 65530 12 0 2 0
0 0 0 0 X 0
1 0 0 0 X 0
0 0 0 0 X 0
1 0 0 0 X 0
0 60000 3 1 X X
1 60000 3 1 X X
repeat (255) C 60000 3 0 X X
0 60000 3 0 39 0
1 60000 3 0 39 0
0 0 0 0 X 0
1 0 0 0 X 0
0 0 0 0 X 0
1 0 0 0 X 0
0 55124 4 1 X X
1 55124 4 1 X X
repeat (255) C 55124 4 0 X X
0 55124 4 0 15 0
1 55124 4 0 15 0
0 0 0 0 X 0
1 0 0 0 X 0
0 0 0 0 X 0
1 0 0 0 X 0
0 14778 5 1 X X
1 14778 5 1 X X
repeat (255) C 14778 5 0 X X
0 14778 5 0 6 0
1 14778 5 0 6 0
*/

/* Test case TestCase8:
clk A R input nroot busy
0 0 0 0 X 0
1 0 0 0 X 0
0 0 0 0 X 0
1 0 0 0 X 0
0 65535 1 1 X X
1 65535 1 1 X X
repeat (255) C 65535 1 0 X X
0 65535 1 0 65535 0
1 65535 1 0 65535 0
0 0 0 0 X 0
1 0 0 0 X 0
0 0 0 0 X 0
1 0 0 0 X 0
0 64000 15 1 X X
1 64000 15 1 X X
repeat (255) C 64000 15 0 X X
0 64000 15 0 2 0
1 64000 15 0 2 0
0 0 0 0 X 0
1 0 0 0 X 0
0 0 0 0 X 0
1 0 0 0 X 0
0 12000 5 1 X X
1 12000 5 1 X X
repeat (255) C 12000 5 0 X X
0 12000 5 0 6 0
1 12000 5 0 6 0
0 0 0 0 X 0
1 0 0 0 X 0
0 0 0 0 X 0
1 0 0 0 X 0
0 65535 15 1 X X
1 65535 15 1 X X
repeat (255) C 65535 15 0 X X
0 65535 15 0 2 0
1 65535 15 0 2 0
*/
