// Digital circuit 03.dig as structural Verilog
module _03 (
  input  [15:0] A,
  input  \input ,
  input  clk,
  input  reset,
  output [17:0] peak
);

  wire and_2_out, and_3_out, comparator_1_gt, comparator_5_gt, comparator_6_eq, comparator_7_gt, d_ff_1_q,
       input_t, isNeg_1, isNeg_2, isNeg_3, xor_1_out, xor_2_out;
  wire [3:0] counter_1_out;
  wire [15:0] _1, _1_neg, _2, _2_neg, _3, _3_neg, add_1_s, add_2_s, add_3_s, multiplexer_1_out,
       multiplexer_2_out, multiplexer_7_out, multiplexer_8_out, neg_1_out, neg_2_out, neg_3_out, S1, S2,
       sub_1_s, sub_2_s;
  wire [16:16] add_3_c_o;
  wire [17:0] register_4_q;

  D_FF d_ff_1 (.D(\input ), .C(clk), .Q(d_ff_1_q));  // open: nQ
  and and_1 (input_t, \input , ~d_ff_1_q);  // And
  Register #(.Bits(16)) register_1 (.D(A), .C(clk), .en(input_t), .Q(_1));
  Comparator #(.Bits(16)) comparator_1 (.a(_1_neg), .b(_2_neg), .gt(comparator_1_gt));  // open: eq, lt
  Add #(.Bits(16)) add_1 (.a(_1_neg), .b(_2_neg), .c_i(1'b0), .s(add_1_s));  // open: c_o
  Comparator #(.Bits(16)) comparator_2 (.a(_1), .b(16'h8000), .gt(isNeg_1));  // open: eq, lt
  Comparator #(.Bits(16)) comparator_3 (.a(_2), .b(16'h8000), .gt(isNeg_2));  // open: eq, lt
  Comparator #(.Bits(16)) comparator_4 (.a(_3), .b(16'h8000), .gt(isNeg_3));  // open: eq, lt
  Multiplexer #(.Bits(16)) multiplexer_1 (.sel(comparator_1_gt), .in_0(_2_neg), .in_1(_1_neg), .out(multiplexer_1_out));
  Multiplexer #(.Bits(16)) multiplexer_2 (.sel(comparator_1_gt), .in_0(_1_neg), .in_1(_2_neg), .out(multiplexer_2_out));
  Register #(.Bits(16)) register_2 (.D(_1), .C(clk), .en(input_t), .Q(_2));
  Sub #(.Bits(16)) sub_1 (.a(multiplexer_1_out), .b(multiplexer_2_out), .c_i(1'b0), .s(sub_1_s));  // open: c_o
  Neg #(.Bits(16)) neg_1 (.in(_1), .out(neg_1_out));
  Multiplexer #(.Bits(16)) multiplexer_3 (.sel(isNeg_1), .in_0(_1), .in_1(neg_1_out), .out(_1_neg));
  Neg #(.Bits(16)) neg_2 (.in(_2), .out(neg_2_out));
  Multiplexer #(.Bits(16)) multiplexer_4 (.sel(isNeg_2), .in_0(_2), .in_1(neg_2_out), .out(_2_neg));
  Neg #(.Bits(16)) neg_3 (.in(_3), .out(neg_3_out));
  Multiplexer #(.Bits(16)) multiplexer_5 (.sel(isNeg_3), .in_0(_3), .in_1(neg_3_out), .out(_3_neg));
  Multiplexer #(.Bits(16)) multiplexer_6 (.sel(xor_1_out), .in_0(sub_1_s), .in_1(add_1_s), .out(S1));
  xor xor_1 (xor_1_out, isNeg_2, isNeg_1);
  Register #(.Bits(16)) register_3 (.D(_2), .C(clk), .en(input_t), .Q(_3));
  Comparator #(.Bits(16)) comparator_5 (.a(_2_neg), .b(_3_neg), .gt(comparator_5_gt));  // open: eq, lt
  Multiplexer #(.Bits(16)) multiplexer_7 (.sel(comparator_5_gt), .in_0(_3_neg), .in_1(_2_neg), .out(multiplexer_7_out));
  Multiplexer #(.Bits(16)) multiplexer_8 (.sel(comparator_5_gt), .in_0(_2_neg), .in_1(_3_neg), .out(multiplexer_8_out));
  Add #(.Bits(16)) add_2 (.a(_2_neg), .b(_3_neg), .c_i(1'b0), .s(add_2_s));  // open: c_o
  Sub #(.Bits(16)) sub_2 (.a(multiplexer_7_out), .b(multiplexer_8_out), .c_i(1'b0), .s(sub_2_s));  // open: c_o
  Add #(.Bits(16)) add_3 (.a(S1), .b(S2), .c_i(1'b0), .s(add_3_s), .c_o(add_3_c_o[16]));
  and and_2 (and_2_out, input_t, ~comparator_6_eq);  // And
  Multiplexer #(.Bits(16)) multiplexer_9 (.sel(xor_2_out), .in_0(sub_2_s), .in_1(add_2_s), .out(S2));
  xor xor_2 (xor_2_out, isNeg_3, isNeg_2);
  Register #(.Bits(18)) register_4 (.D({1'b0, add_3_c_o[16], add_3_s}), .C(clk), .en(and_3_out), .Q(register_4_q));
  Counter #(.Bits(4)) counter_1 (.en(and_2_out), .C(clk), .clr(1'b0), .out(counter_1_out));  // open: ovf
  and and_3 (and_3_out, comparator_6_eq, comparator_7_gt);
  Comparator #(.Bits(4)) comparator_6 (.a(counter_1_out), .b(4'b0011), .eq(comparator_6_eq));  // open: gt, lt
  Comparator #(.Bits(18)) comparator_7 (
    .a({1'b0, add_3_c_o[16], add_3_s}), .b(register_4_q), .gt(comparator_7_gt));  // open: eq, lt
  Multiplexer #(.Bits(18)) multiplexer_10 (.sel(comparator_6_eq), .in_0({18{1'b0}}), .in_1(register_4_q), .out(peak));

  // Notes on the sheet:
  //   Memory
  //   Differences
  //   Negative Handler
  //   Peak Handler
endmodule

/* Test case Testcase1:
clk A input reset peak
0 0 0 0 0
1 0 0 0 0
0 0 0 1 0
1 0 0 1 0
0 0  0 0 0
1 0  0 0 0
0 5 1 0 X
1 5 1 0 X
0 0 0 0 X
1 0 0 0 X
0 1 1 0 X
1 1 1 0 X
0 0 0 0 X
1 0 0 0 X
0 0 0 0 X
1 0 0 0 X
0 2 1 0 X
1 2 1 0 X
0 0 0 0 X
1 0 0 0 X
0  0 0 0 5
1  0 0 0 5
0 10 1 0 X
1 10 1 0 X
0 0 0 0 X
1 0 0 0 9
0  0 0 0 9
1  0 0 0 9
0 3 1 0 X
1 3 1 0 X
0 0 0 0 X
1 0 0 0 15
0  0 0 0 15
1  0 0 0 15
0 65526 1 0 X
1 65526 1 0 X
0 0 0 0 X
1 0 0 0 20
0  0 0 0 20
1  0 0 0 20
0 2 1 0 X
1 2 1 0 X
0 0 0 0 X
1 0 0 0 25
0  0 0 0 25
1  0 0 0 25
0 4 1 0 X
1 4 1 0 X
0 0 0 0 X
1 0 0 0 25
0  0 0 0 25
1  0 0 0 25
0 1 1 0 X
1 1 1 0 X
0 0 0 0 X
1 0 0 0 25
0  0 0 0 25
1  0 0 0 25
0 2 1 0 X
1 2 1 0 X
0 0 0 0 X
1 0 0 0 25
*/

/* Test case Testcase3:
clk A input reset peak
0 0 0 0 0
1 0 0 0 0
0 0 0 1 0
1 0 0 1 0
0 0  0 0 0
1 0  0 0 0
0 9924 1 0 X
1 9924 1 0 X
0 0 0 0 X
1 0 0 0 X
0 1714 1 0 X
1 1714 1 0 X
0 0 0 0 X
1 0 0 0 X
0 0 0 0 X
1 0 0 0 X
0 19734 1 0 X
1 19734 1 0 X
0 0 0 0 X
1 0 0 0 X
0  0 0 0 26230
1  0 0 0 26230
0 14144 1 0 X
1 14144 1 0 X
0 0 0 0 X
1 0 0 0 26230
0  0 0 0 26230
1  0 0 0 26230
0 6348 1 0 X
1 6348 1 0 X
0 0 0 0 X
1 0 0 0 26230
0  0 0 0 26230
1  0 0 0 26230
0 29200 1 0 X
1 29200 1 0 X
0 0 0 0 X
1 0 0 0 30648
0  0 0 0 30648
1  0 0 0 30648
0 13658 1 0 X
1 13658 1 0 X
0 0 0 0 X
1 0 0 0 38394
0  0 0 0 38394
1  0 0 0 38394
0 20001 1 0 X
1 20001 1 0 X
0 0 0 0 X
1 0 0 0 38394
0  0 0 0 38394
1  0 0 0 38394
0 23323 1 0 X
1 23323 1 0 X
0 0 0 0 X
1 0 0 0 38394
0  0 0 0 38394
1  0 0 0 38394
0 15516 1 0 X
1 15516 1 0 X
0 0 0 0 X
1 0 0 0 38394
0  0 0 0 38394
1  0 0 0 38394
0 26104 1 0 X
1 26104 1 0 X
0 0 0 0 X
1 0 0 0 38394
0  0 0 0 38394
1  0 0 0 38394
0 23576 1 0 X
1 23576 1 0 X
0 0 0 0 X
1 0 0 0 38394
0  0 0 0 38394
1  0 0 0 38394
0 15152 1 0 X
1 15152 1 0 X
0 0 0 0 X
1 0 0 0 38394
0  0 0 0 38394
1  0 0 0 38394
0 9762 1 0 X
1 9762 1 0 X
0 0 0 0 X
1 0 0 0 38394
0  0 0 0 38394
1  0 0 0 38394
0 3599 1 0 X
1 3599 1 0 X
0 0 0 0 X
1 0 0 0 38394
0  0 0 0 38394
1  0 0 0 38394
0 16576 1 0 X
1 16576 1 0 X
0 0 0 0 X
1 0 0 0 38394
0  0 0 0 38394
1  0 0 0 38394
0 30162 1 0 X
1 30162 1 0 X
0 0 0 0 X
1 0 0 0 38394
0  0 0 0 38394
1  0 0 0 38394
0 30934 1 0 X
1 30934 1 0 X
0 0 0 0 X
1 0 0 0 38394
0  0 0 0 38394
1  0 0 0 38394
0 31029 1 0 X
1 31029 1 0 X
0 0 0 0 X
1 0 0 0 38394
0  0 0 0 38394
1  0 0 0 38394
0 18783 1 0 X
1 18783 1 0 X
0 0 0 0 X
1 0 0 0 38394
0  0 0 0 38394
1  0 0 0 38394
0 1881 1 0 X
1 1881 1 0 X
0 0 0 0 X
1 0 0 0 38394
0  0 0 0 38394
1  0 0 0 38394
0 10695 1 0 X
1 10695 1 0 X
0 0 0 0 X
1 0 0 0 38394
0  0 0 0 38394
1  0 0 0 38394
0 7756 1 0 X
1 7756 1 0 X
0 0 0 0 X
1 0 0 0 38394
0  0 0 0 38394
1  0 0 0 38394
0 14129 1 0 X
1 14129 1 0 X
0 0 0 0 X
1 0 0 0 38394
0  0 0 0 38394
1  0 0 0 38394
0 30596 1 0 X
1 30596 1 0 X
0 0 0 0 X
1 0 0 0 38394
0  0 0 0 38394
1  0 0 0 38394
0 21070 1 0 X
1 21070 1 0 X
0 0 0 0 X
1 0 0 0 38394
0  0 0 0 38394
1  0 0 0 38394
0 15427 1 0 X
1 15427 1 0 X
0 0 0 0 X
1 0 0 0 38394
0  0 0 0 38394
1  0 0 0 38394
0 2565 1 0 X
1 2565 1 0 X
0 0 0 0 X
1 0 0 0 38394
0  0 0 0 38394
1  0 0 0 38394
0 24554 1 0 X
1 24554 1 0 X
0 0 0 0 X
1 0 0 0 38394
0  0 0 0 38394
1  0 0 0 38394
0 25370 1 0 X
1 25370 1 0 X
0 0 0 0 X
1 0 0 0 38394
0  0 0 0 38394
1  0 0 0 38394
0 9273 1 0 X
1 9273 1 0 X
0 0 0 0 X
1 0 0 0 38394
0  0 0 0 38394
1  0 0 0 38394
0 8302 1 0 X
1 8302 1 0 X
0 0 0 0 X
1 0 0 0 38394
0  0 0 0 38394
1  0 0 0 38394
0 3282 1 0 X
1 3282 1 0 X
0 0 0 0 X
1 0 0 0 38394
0  0 0 0 38394
1  0 0 0 38394
0 25633 1 0 X
1 25633 1 0 X
0 0 0 0 X
1 0 0 0 38394
0  0 0 0 38394
1  0 0 0 38394
0 13448 1 0 X
1 13448 1 0 X
0 0 0 0 X
1 0 0 0 38394
0  0 0 0 38394
1  0 0 0 38394
0 5516 1 0 X
1 5516 1 0 X
0 0 0 0 X
1 0 0 0 38394
0  0 0 0 38394
1  0 0 0 38394
0 31976 1 0 X
1 31976 1 0 X
0 0 0 0 X
1 0 0 0 38394
0  0 0 0 38394
1  0 0 0 38394
0 24271 1 0 X
1 24271 1 0 X
0 0 0 0 X
1 0 0 0 38394
0  0 0 0 38394
1  0 0 0 38394
0 6215 1 0 X
1 6215 1 0 X
0 0 0 0 X
1 0 0 0 38394
0  0 0 0 38394
1  0 0 0 38394
0 10282 1 0 X
1 10282 1 0 X
0 0 0 0 X
1 0 0 0 38394
0  0 0 0 38394
1  0 0 0 38394
0 28448 1 0 X
1 28448 1 0 X
0 0 0 0 X
1 0 0 0 38394
0  0 0 0 38394
1  0 0 0 38394
0 19282 1 0 X
1 19282 1 0 X
0 0 0 0 X
1 0 0 0 38394
0  0 0 0 38394
1  0 0 0 38394
0 16410 1 0 X
1 16410 1 0 X
0 0 0 0 X
1 0 0 0 38394
0  0 0 0 38394
1  0 0 0 38394
0 4699 1 0 X
1 4699 1 0 X
0 0 0 0 X
1 0 0 0 38394
0  0 0 0 38394
1  0 0 0 38394
0 17855 1 0 X
1 17855 1 0 X
0 0 0 0 X
1 0 0 0 38394
0  0 0 0 38394
1  0 0 0 38394
0 7295 1 0 X
1 7295 1 0 X
0 0 0 0 X
1 0 0 0 38394
0  0 0 0 38394
1  0 0 0 38394
0 5567 1 0 X
1 5567 1 0 X
0 0 0 0 X
1 0 0 0 38394
0  0 0 0 38394
1  0 0 0 38394
0 5318 1 0 X
1 5318 1 0 X
0 0 0 0 X
1 0 0 0 38394
0  0 0 0 38394
1  0 0 0 38394
0 7523 1 0 X
1 7523 1 0 X
0 0 0 0 X
1 0 0 0 38394
0  0 0 0 38394
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*/

/* Test case Testcase6:
clk A input reset peak
0 0 0 0 0
1 0 0 0 0
0 0 0 1 0
1 0 0 1 0
0 0  0 0 0
1 0  0 0 0
0 64563 1 0 X
1 64563 1 0 X
0 0 0 0 X
1 0 0 0 X
0 64536 1 0 X
1 64536 1 0 X
0 0 0 0 X
1 0 0 0 X
0 0 0 0 X
1 0 0 0 X
0 64709 1 0 X
1 64709 1 0 X
0 0 0 0 X
1 0 0 0 X
0  0 0 0 200
1  0 0 0 200
0 64724 1 0 X
1 64724 1 0 X
0 0 0 0 X
1 0 0 0 200
0  0 0 0 200
1  0 0 0 200
0 64709 1 0 X
1 64709 1 0 X
0 0 0 0 X
1 0 0 0 200
0  0 0 0 200
1  0 0 0 200
0 64804 1 0 X
1 64804 1 0 X
0 0 0 0 X
1 0 0 0 200
0  0 0 0 200
1  0 0 0 200
0 64890 1 0 X
1 64890 1 0 X
0 0 0 0 X
1 0 0 0 200
0  0 0 0 200
1  0 0 0 200
0 64804 1 0 X
1 64804 1 0 X
0 0 0 0 X
1 0 0 0 200
0  0 0 0 200
1  0 0 0 200
0 64917 1 0 X
1 64917 1 0 X
0 0 0 0 X
1 0 0 0 200
0  0 0 0 200
1  0 0 0 200
0 64968 1 0 X
1 64968 1 0 X
0 0 0 0 X
1 0 0 0 200
0  0 0 0 200
1  0 0 0 200
0 64917 1 0 X
1 64917 1 0 X
0 0 0 0 X
1 0 0 0 200
0  0 0 0 200
1  0 0 0 200
0 65085 1 0 X
1 65085 1 0 X
0 0 0 0 X
1 0 0 0 219
0  0 0 0 219
1  0 0 0 219
0 65153 1 0 X
1 65153 1 0 X
0 0 0 0 X
1 0 0 0 236
0  0 0 0 236
1  0 0 0 236
0 65085 1 0 X
1 65085 1 0 X
0 0 0 0 X
1 0 0 0 236
0  0 0 0 236
1  0 0 0 236
0 65242 1 0 X
1 65242 1 0 X
0 0 0 0 X
1 0 0 0 236
0  0 0 0 236
1  0 0 0 236
0 65299 1 0 X
1 65299 1 0 X
0 0 0 0 X
1 0 0 0 236
0  0 0 0 236
1  0 0 0 236
0 65242 1 0 X
1 65242 1 0 X
0 0 0 0 X
1 0 0 0 236
0  0 0 0 236
1  0 0 0 236
0 65411 1 0 X
1 65411 1 0 X
0 0 0 0 X
1 0 0 0 236
0  0 0 0 236
1  0 0 0 236
0 65453 1 0 X
1 65453 1 0 X
0 0 0 0 X
1 0 0 0 236
0  0 0 0 236
1  0 0 0 236
0 65411 1 0 X
1 65411 1 0 X
0 0 0 0 X
1 0 0 0 236
0  0 0 0 236
1  0 0 0 236
0 152 1 0 X
1 152 1 0 X
0 0 0 0 X
1 0 0 0 319
0  0 0 0 319
1  0 0 0 319
0 175 1 0 X
1 175 1 0 X
0 0 0 0 X
1 0 0 0 319
0  0 0 0 319
1  0 0 0 319
0 152 1 0 X
1 152 1 0 X
0 0 0 0 X
1 0 0 0 319
0  0 0 0 319
1  0 0 0 319
0 546 1 0 X
1 546 1 0 X
0 0 0 0 X
1 0 0 0 417
0  0 0 0 417
1  0 0 0 417
0 612 1 0 X
1 612 1 0 X
0 0 0 0 X
1 0 0 0 460
0  0 0 0 460
1  0 0 0 460
0 546 1 0 X
1 546 1 0 X
0 0 0 0 X
1 0 0 0 460
0  0 0 0 460
1  0 0 0 460
0 947 1 0 X
1 947 1 0 X
0 0 0 0 X
1 0 0 0 467
0  0 0 0 467
1  0 0 0 467
0 1033 1 0 X
1 1033 1 0 X
0 0 0 0 X
1 0 0 0 487
0  0 0 0 487
1  0 0 0 487
0 947 1 0 X
1 947 1 0 X
0 0 0 0 X
1 0 0 0 487
0  0 0 0 487
1  0 0 0 487
0 1335 1 0 X
1 1335 1 0 X
0 0 0 0 X
1 0 0 0 487
0  0 0 0 487
1  0 0 0 487
0 1351 1 0 X
1 1351 1 0 X
0 0 0 0 X
1 0 0 0 487
0  0 0 0 487
1  0 0 0 487
0 1335 1 0 X
1 1335 1 0 X
0 0 0 0 X
1 0 0 0 487
0  0 0 0 487
1  0 0 0 487
0 1847 1 0 X
1 1847 1 0 X
0 0 0 0 X
1 0 0 0 528
0  0 0 0 528
1  0 0 0 528
0 1884 1 0 X
1 1884 1 0 X
0 0 0 0 X
1 0 0 0 549
0  0 0 0 549
1  0 0 0 549
0 1847 1 0 X
1 1847 1 0 X
0 0 0 0 X
1 0 0 0 549
0  0 0 0 549
1  0 0 0 549
0 2409 1 0 X
1 2409 1 0 X
0 0 0 0 X
1 0 0 0 599
0  0 0 0 599
1  0 0 0 599
0 2440 1 0 X
1 2440 1 0 X
0 0 0 0 X
1 0 0 0 599
0  0 0 0 599
1  0 0 0 599
0 2409 1 0 X
1 2409 1 0 X
0 0 0 0 X
1 0 0 0 599
0  0 0 0 599
1  0 0 0 599
0 3004 1 0 X
1 3004 1 0 X
0 0 0 0 X
1 0 0 0 626
0  0 0 0 626
1  0 0 0 626
0 3099 1 0 X
1 3099 1 0 X
0 0 0 0 X
1 0 0 0 690
0  0 0 0 690
1  0 0 0 690
0 3004 1 0 X
1 3004 1 0 X
0 0 0 0 X
1 0 0 0 690
0  0 0 0 690
1  0 0 0 690
0 3576 1 0 X
1 3576 1 0 X
0 0 0 0 X
1 0 0 0 690
0  0 0 0 690
1  0 0 0 690
0 3581 1 0 X
1 3581 1 0 X
0 0 0 0 X
1 0 0 0 690
0  0 0 0 690
1  0 0 0 690
0 3576 1 0 X
1 3576 1 0 X
0 0 0 0 X
1 0 0 0 690
0  0 0 0 690
1  0 0 0 690
0 4285 1 0 X
1 4285 1 0 X
0 0 0 0 X
1 0 0 0 714
0  0 0 0 714
1  0 0 0 714
0 4345 1 0 X
1 4345 1 0 X
0 0 0 0 X
1 0 0 0 769
0  0 0 0 769
1  0 0 0 769
0 4285 1 0 X
1 4285 1 0 X
0 0 0 0 X
1 0 0 0 769
0  0 0 0 769
1  0 0 0 769
0 4982 1 0 X
1 4982 1 0 X
0 0 0 0 X
1 0 0 0 769
0  0 0 0 769
1  0 0 0 769
0 5014 1 0 X
1 5014 1 0 X
0 0 0 0 X
1 0 0 0 769
0  0 0 0 769
1  0 0 0 769
0 4982 1 0 X
1 4982 1 0 X
0 0 0 0 X
1 0 0 0 769
0  0 0 0 769
1  0 0 0 769
0 5798 1 0 X
1 5798 1 0 X
0 0 0 0 X
1 0 0 0 848
0  0 0 0 848
1  0 0 0 848
0 5852 1 0 X
1 5852 1 0 X
0 0 0 0 X
1 0 0 0 870
0  0 0 0 870
1  0 0 0 870
0 5798 1 0 X
1 5798 1 0 X
0 0 0 0 X
1 0 0 0 870
0  0 0 0 870
1  0 0 0 870
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*/
