// Digital circuit 2016_01.dig as structural Verilog
module _2016_01 (
  input  Aware,
  input  Walk,
  input  Drive,
  input  Clock
);

  wire and_1_out, aware_t, comparator_1_eq, d_ff_1_q, d_ff_2_q, d_ff_3_q, d_ff_4_q, decoder_1_out_0,
       decoder_1_out_1, decoder_1_out_2, decoder_1_out_3, decoder_2_out_0, decoder_2_out_1, decoder_2_out_2,
       decoder_2_out_3, drive_t, Green_drive, Green_walk, multiplexer_4_out, multiplexer_5_out,
       multiplexer_6_out, multiplexer_7_out, multiplexer_8_out, multiplexer_9_out, multiplexer_10_out,
       multiplexer_11_out, multiplexer_12_out, multiplexer_13_out, multiplexer_14_out, multiplexer_15_out,
       not_1_out, not_2_out, or_1_out, or_2_out, or_3_out, Red_drive, Red_walk, walk_t, Yellow_drive,
       Yellow_walk;
  wire [1:0] Drive_seq_d, drive_sig, Walk_seq_d, walk_sig;
  wire [2:0] counter_1_out, counterpreset_1_out, counterpreset_2_out, seq;

  Multiplexer #(.Bits(3)) multiplexer_1 (.sel(drive_t), .in_0(3'b000), .in_1(3'b100), .out(seq));
  or or_1 (or_1_out, walk_t, drive_t);
  or or_2 (or_2_out, and_1_out, or_1_out);
  and and_1 (and_1_out, or_2_out, ~aware_t, not_2_out);  // And
  not not_1 (not_1_out, or_2_out);
  Counter #(.Bits(3)) counter_1 (.en(or_2_out), .C(Clock), .clr(not_1_out), .out(counter_1_out));  // open: ovf
  Comparator #(.Bits(3)) comparator_1 (.a(counter_1_out), .b(3'b100), .eq(comparator_1_eq));  // open: gt, lt
  D_FF d_ff_1 (.D(Walk), .C(Clock), .Q(d_ff_1_q));  // open: nQ
  or or_3 (or_3_out, Aware, walk_t, drive_t);
  D_FF d_ff_2 (.D(Drive), .C(Clock), .Q(d_ff_2_q));  // open: nQ
  not not_2 (not_2_out, comparator_1_eq);
  D_FF d_ff_3 (.D(d_ff_1_q), .C(Clock), .Q(d_ff_3_q));  // open: nQ
  D_FF d_ff_4 (.D(d_ff_2_q), .C(Clock), .Q(d_ff_4_q));  // open: nQ
  and and_2 (walk_t, d_ff_1_q, ~d_ff_3_q);  // And
  Register register_1 (.D(Aware), .C(Clock), .en(or_3_out), .Q(aware_t));
  and and_3 (drive_t, d_ff_2_q, ~d_ff_4_q);  // And
  CounterPreset #(.Bits(3)) counterpreset_1 (
    .en(and_1_out), .C(Clock), .dir(1'b0), .in(seq), .ld(or_1_out), .clr(1'b0), .out(counterpreset_1_out));  // open: ovf
  CounterPreset #(.Bits(3)) counterpreset_2 (
    .en(and_1_out), .C(Clock), .dir(1'b0), .in(seq), .ld(or_1_out), .clr(1'b0), .out(counterpreset_2_out));  // open: ovf
  ROM #(.AddrBits(3), .isProgramMemory("true"), .Bits(2)) Walk_seq (
    .A(counterpreset_1_out), .sel(1'b1), .D(Walk_seq_d));
  ROM #(.AddrBits(3), .isProgramMemory("true"), .Bits(2)) Drive_seq (
    .A(counterpreset_2_out), .sel(1'b1), .D(Drive_seq_d));
  Multiplexer #(.Bits(2)) multiplexer_2 (.sel(aware_t), .in_0(Walk_seq_d), .in_1(2'b00), .out(walk_sig));
  Multiplexer #(.Bits(2)) multiplexer_3 (.sel(aware_t), .in_0(Drive_seq_d), .in_1(2'b00), .out(drive_sig));
  Decoder #(.Selector_Bits(2)) decoder_1 (
    .sel(drive_sig), .out_0(decoder_1_out_0), .out_1(decoder_1_out_1), .out_2(decoder_1_out_2),
    .out_3(decoder_1_out_3));
  LED led_1 (.in(Green_drive));
  Multiplexer multiplexer_4 (
    .sel(decoder_1_out_0), .in_0(decoder_1_out_3), .in_1(Green_drive), .out(multiplexer_4_out));
  Multiplexer multiplexer_5 (
    .sel(decoder_1_out_0), .in_0(decoder_1_out_2), .in_1(Yellow_drive), .out(multiplexer_5_out));
  Multiplexer multiplexer_6 (.sel(decoder_1_out_0), .in_0(decoder_1_out_1), .in_1(Red_drive), .out(multiplexer_6_out));
  LED led_2 (.in(Yellow_drive));
  LED led_3 (.in(Red_drive));
  Multiplexer multiplexer_7 (.sel(aware_t), .in_0(multiplexer_4_out), .in_1(1'b0), .out(multiplexer_7_out));
  Multiplexer multiplexer_8 (.sel(aware_t), .in_0(multiplexer_5_out), .in_1(1'b1), .out(multiplexer_8_out));
  Multiplexer multiplexer_9 (.sel(aware_t), .in_0(multiplexer_6_out), .in_1(1'b0), .out(multiplexer_9_out));
  Register register_2 (.D(multiplexer_7_out), .C(Clock), .en(1'b1), .Q(Green_drive));
  Register register_3 (.D(multiplexer_8_out), .C(Clock), .en(1'b1), .Q(Yellow_drive));
  Register register_4 (.D(multiplexer_9_out), .C(Clock), .en(1'b1), .Q(Red_drive));
  LED led_4 (.in(Green_walk));
  LED led_5 (.in(Yellow_walk));
  LED led_6 (.in(Red_walk));
  Decoder #(.Selector_Bits(2)) decoder_2 (
    .sel(walk_sig), .out_0(decoder_2_out_0), .out_1(decoder_2_out_1), .out_2(decoder_2_out_2),
    .out_3(decoder_2_out_3));
  Multiplexer multiplexer_10 (
    .sel(decoder_2_out_0), .in_0(decoder_2_out_3), .in_1(Green_walk), .out(multiplexer_10_out));
  Multiplexer multiplexer_11 (
    .sel(decoder_2_out_0), .in_0(decoder_2_out_2), .in_1(Yellow_walk), .out(multiplexer_11_out));
  Multiplexer multiplexer_12 (.sel(decoder_2_out_0), .in_0(decoder_2_out_1), .in_1(Red_walk), .out(multiplexer_12_out));
  Multiplexer multiplexer_13 (.sel(aware_t), .in_0(multiplexer_10_out), .in_1(1'b0), .out(multiplexer_13_out));
  Multiplexer multiplexer_14 (.sel(aware_t), .in_0(multiplexer_11_out), .in_1(1'b1), .out(multiplexer_14_out));
  Multiplexer multiplexer_15 (.sel(aware_t), .in_0(multiplexer_12_out), .in_1(1'b0), .out(multiplexer_15_out));
  Register register_5 (.D(multiplexer_13_out), .C(Clock), .en(1'b1), .Q(Green_walk));
  Register register_6 (.D(multiplexer_14_out), .C(Clock), .en(1'b1), .Q(Yellow_walk));
  Register register_7 (.D(multiplexer_15_out), .C(Clock), .en(1'b1), .Q(Red_walk));

  // Other names for the same wires on the sheet: clk = Clock

  // Notes on the sheet:
  //   contents of Walk_seq (hex, n*v repeats v):
  //   1,1,1,3,0,2,1,1
  //   contents of Drive_seq (hex, n*v repeats v):
  //   0,2,5*1,3
endmodule
