// Digital circuit 2016_02.dig as structural Verilog
module _2016_02 (
  input  [3:0] A
);

  wire [3:0] div_1_q, div_2_q, div_2_r;
  wire [7:0] div_1_r, mul_1_mul;
  wire [7:4] div_1_q_2, div_2_q_2, div_2_r_2;

  Mul #(.Bits(4)) mul_1 (.a(A), .b(4'b1001), .mul(mul_1_mul));
  Div #(.Bits(8)) div_1 (.a(mul_1_mul), .b(8'h64), .q({div_1_q_2, div_1_q}), .r(div_1_r));
  Seven_Seg_Hex seven_seg_hex_1 (.d(div_1_q), .dp(1'b0));
  Div #(.Bits(8)) div_2 (.a(div_1_r), .b(8'ha), .q({div_2_q_2, div_2_q}), .r({div_2_r_2, div_2_r}));
  Seven_Seg_Hex seven_seg_hex_2 (.d(div_2_q), .dp(1'b0));
  Seven_Seg_Hex seven_seg_hex_3 (.d(div_2_r), .dp(1'b0));
endmodule
