// Digital circuit 2020_01.dig as structural Verilog
module _2020_01 (
  input  Start,
  input  Clock,
  input  [7:0] A,
  input  [7:0] B,
  output Busy,
  output [7:0] Output
);

  wire comparator_1_gt, comparator_2_eq, d_ff_1_q, d_ff_2_q, not_1_out, or_1_out, Start_t;
  wire [7:0] a_t, b_t, multiplexer_1_out, multiplexer_2_out, multiplexer_3_out, multiplexer_4_out, sub_1_s,
       sub_2_s;

  D_FF d_ff_1 (.D(Start), .C(Clock), .Q(d_ff_1_q));  // open: nQ
  D_FF d_ff_2 (.D(d_ff_1_q), .C(Clock), .Q(d_ff_2_q));  // open: nQ
  and and_1 (Start_t, d_ff_1_q, ~d_ff_2_q);  // And
  Sub #(.Bits(8)) sub_1 (.a(a_t), .b(b_t), .c_i(1'b0), .s(sub_1_s));  // open: c_o
  Comparator #(.Bits(8)) comparator_1 (.a(a_t), .b(b_t), .gt(comparator_1_gt));  // open: eq, lt
  Sub #(.Bits(8)) sub_2 (.a(b_t), .b(a_t), .c_i(1'b0), .s(sub_2_s));  // open: c_o
  Multiplexer #(.Bits(8)) multiplexer_1 (.sel(comparator_1_gt), .in_0(a_t), .in_1(sub_1_s), .out(multiplexer_1_out));
  Multiplexer #(.Bits(8)) multiplexer_2 (.sel(comparator_1_gt), .in_0(sub_2_s), .in_1(b_t), .out(multiplexer_2_out));
  Multiplexer #(.Bits(8)) multiplexer_3 (.sel(Start_t), .in_0(multiplexer_1_out), .in_1(A), .out(multiplexer_3_out));
  or or_1 (or_1_out, Start_t, Busy);
  Multiplexer #(.Bits(8)) multiplexer_4 (.sel(Start_t), .in_0(multiplexer_2_out), .in_1(B), .out(multiplexer_4_out));
  Comparator #(.Bits(8)) comparator_2 (.a(a_t), .b(b_t), .eq(comparator_2_eq));  // open: gt, lt
  Register #(.Bits(8)) register_1 (.D(multiplexer_3_out), .C(Clock), .en(or_1_out), .Q(a_t));
  Register #(.Bits(8)) register_2 (.D(multiplexer_4_out), .C(Clock), .en(or_1_out), .Q(b_t));
  not not_1 (not_1_out, comparator_2_eq);
  Multiplexer multiplexer_5 (.sel(Start_t), .in_0(not_1_out), .in_1(1'b1), .out(Busy));
  Multiplexer #(.Bits(8)) multiplexer_6 (.sel(Busy), .in_0(a_t), .in_1({8{1'b0}}), .out(Output));

  // Other names for the same wires on the sheet: clk = Clock
endmodule
