// Digital circuit 2020_02.dig as structural Verilog
module _2020_02 (
  input  [3:0] A,
  input  [3:0] B,
  output [3:0] Q,
  output [3:0] R
);

  wire comparator_1_eq, not_1_out;
  wire [3:0] div_1_q;

  Div #(.Bits(4)) div_1 (.a(A), .b(B), .q(div_1_q), .r(R));
  Comparator #(.Bits(4)) comparator_1 (.a(B), .b(4'b0000), .eq(comparator_1_eq));  // open: gt, lt
  Multiplexer #(.Bits(4)) multiplexer_1 (.sel(not_1_out), .in_0(4'b0000), .in_1(div_1_q), .out(Q));
  not not_1 (not_1_out, comparator_1_eq);
endmodule
