// Digital circuit 2021_01.dig as structural Verilog
module _2021_01 (
  input  [7:0] A,
  input  Add,
  input  Reset,
  input  Clock,
  output [11:0] \output 
);

  wire add_1_c_o, add_t, d_ff_1_q, d_ff_2_q, or_1_out;
  wire [11:0] add_2_s, div_1_q, div_1_r, div_2_q, div_2_r, div_3_q, div_3_r, multiplexer_1_out;

  Add #(.Bits(8)) add_1 (.a(A), .b(\output [7:0]), .c_i(1'b0), .s(add_2_s[7:0]), .c_o(add_1_c_o));
  Add #(.Bits(4)) add_2 (.a(4'b0000), .b(\output [11:8]), .c_i(add_1_c_o), .s(add_2_s[11:8]));  // open: c_o
  Multiplexer #(.Bits(12)) multiplexer_1 (.sel(Reset), .in_0(add_2_s), .in_1({12{1'b0}}), .out(multiplexer_1_out));
  or or_1 (or_1_out, Reset, add_t);
  Register #(.Bits(12)) register_1 (.D(multiplexer_1_out), .C(Clock), .en(or_1_out), .Q(\output ));
  D_FF d_ff_1 (.D(Add), .C(Clock), .Q(d_ff_1_q));  // open: nQ
  D_FF d_ff_2 (.D(d_ff_1_q), .C(Clock), .Q(d_ff_2_q));  // open: nQ
  and and_1 (add_t, d_ff_1_q, ~d_ff_2_q);  // And
  Seven_Seg_Hex seven_seg_hex_1 (.d(div_1_q[3:0]), .dp(1'b0));
  Div #(.Bits(12)) div_1 (.a(\output ), .b(12'h3e8), .q(div_1_q), .r(div_1_r));
  Seven_Seg_Hex seven_seg_hex_2 (.d(div_2_q[3:0]), .dp(1'b0));
  Div #(.Bits(12)) div_2 (.a(div_1_r), .b(12'h64), .q(div_2_q), .r(div_2_r));
  Seven_Seg_Hex seven_seg_hex_3 (.d(div_3_q[3:0]), .dp(1'b0));
  Div #(.Bits(12)) div_3 (.a(div_2_r), .b(12'ha), .q(div_3_q), .r(div_3_r));
  Seven_Seg_Hex seven_seg_hex_4 (.d(div_3_r[3:0]), .dp(1'b0));

  // Other names for the same wires on the sheet: clk = Clock

  // Notes on the sheet:
  //   Clock: Hz: 200
  //   Adder
  //   Display
endmodule
