// Digital circuit 2021_02.dig as structural Verilog
module _2021_02 (
  input  Count,
  input  Clock,
  output Output
);

  wire and_2_out, comparator_1_eq, comparator_3_gt, Count_t, d_ff_1_q, d_ff_2_q, not_1_out, or_1_out,
       or_2_out;
  wire [3:0] add_1_s, div_1_q, div_1_r, multiplexer_1_out, multiplexer_2_out, \reg ;

  D_FF d_ff_1 (.D(Count), .C(Clock), .Q(d_ff_1_q));  // open: nQ
  D_FF d_ff_2 (.D(d_ff_1_q), .C(Clock), .Q(d_ff_2_q));  // open: nQ
  and and_1 (Count_t, d_ff_1_q, ~d_ff_2_q);  // And
  Add #(.Bits(4)) add_1 (.a(\reg ), .b(4'b0011), .c_i(1'b0), .s(add_1_s));  // open: c_o
  Comparator #(.Bits(4)) comparator_1 (.a(\reg ), .b(4'b0000), .eq(comparator_1_eq));  // open: gt, lt
  Multiplexer #(.Bits(4)) multiplexer_1 (.sel(or_1_out), .in_0(add_1_s), .in_1(4'b0011), .out(multiplexer_1_out));
  or or_1 (or_1_out, comparator_1_eq, and_2_out);
  or or_2 (or_2_out, Count_t, comparator_1_eq);
  and and_2 (and_2_out, Count_t, Output);
  Register #(.Bits(4)) register_1 (.D(multiplexer_1_out), .C(Clock), .en(or_2_out), .Q(\reg ));
  Div #(.Bits(4)) div_1 (.a(\reg ), .b(4'b1010), .q(div_1_q), .r(div_1_r));
  Comparator #(.Bits(4)) comparator_2 (.a(\reg ), .b(4'b1111), .eq(Output));  // open: gt, lt
  Seven_Seg_Hex seven_seg_hex_1 (.d(div_1_q), .dp(1'b0));
  Comparator #(.Bits(4)) comparator_3 (.a(\reg ), .b(4'b1001), .gt(comparator_3_gt));  // open: eq, lt
  Seven_Seg_Hex seven_seg_hex_2 (.d(multiplexer_2_out), .dp(1'b0));
  not not_1 (not_1_out, comparator_3_gt);
  Multiplexer #(.Bits(4)) multiplexer_2 (.sel(not_1_out), .in_0(div_1_r), .in_1(\reg ), .out(multiplexer_2_out));

  // Other names for the same wires on the sheet: clk = Clock
endmodule
