// Digital circuit 2 4 2 1 Code.dig as structural Verilog
module _2_4_2_1_Code (
  input  A,
  input  B,
  input  C,
  input  D,
  input  [1:0] S,
  output [3:0] E
);

  wire and_1_out, and_2_out, and_3_out, and_4_out, and_5_out, and_6_out, not_1_out, not_2_out, not_3_out,
       not_4_out, not_5_out;
  wire [3:1] or_1_out;
  wire [3:3] and_7_out;

  not not_1 (not_1_out, B);
  not not_2 (not_2_out, C);
  not not_3 (not_3_out, D);
  and and_1 (and_1_out, B, D);
  and and_2 (and_2_out, B, C);
  and and_3 (and_3_out, B, not_3_out);
  and and_4 (and_4_out, B, C);
  and and_5 (and_5_out, not_1_out, C);
  and and_6 (and_6_out, B, not_2_out, D);
  or or_1 (or_1_out[3], A, and_1_out, and_2_out);
  or or_2 (or_1_out[2], A, and_3_out, and_4_out);
  or or_3 (or_1_out[1], A, and_5_out, and_6_out);
  not not_4 (not_4_out, S[1]);
  not not_5 (not_5_out, S[0]);
  and and_7 (and_7_out[3], S[1], not_5_out);
  assign E = {or_1_out, D} & {4{and_7_out[3]}};  // And and_8, 4 bits wide
endmodule
