// Digital circuit Template-03.dig as structural Verilog
module Template_03 (
  input  [3:0] In,
  input  [1:0] Selector,
  output [3:0] Output
);

  wire [3:0] _2_4_2_1_code_1_e, _6_4_2__3_code_1_e, cyclic_1_e, excess_3_1_e;

  Excess_3 excess_3_1 (.A(In[3]), .B(In[2]), .C(In[1]), .D(In[0]), .S(Selector), .E(excess_3_1_e));
  Cyclic cyclic_1 (.A(In[3]), .B(In[2]), .C(In[1]), .D(In[0]), .S(Selector), .E(cyclic_1_e));
  _2_4_2_1_Code _2_4_2_1_code_1 (.A(In[3]), .B(In[2]), .C(In[1]), .D(In[0]), .S(Selector), .E(_2_4_2_1_code_1_e));
  _6_4_2__3_Code _6_4_2__3_code_1 (.A(In[3]), .B(In[2]), .C(In[1]), .D(In[0]), .S(Selector), .E(_6_4_2__3_code_1_e));
  assign Output = excess_3_1_e | cyclic_1_e | _2_4_2_1_code_1_e | _6_4_2__3_code_1_e;  // Or or_1, 4 bits wide
endmodule
