// Digital circuit Template-04.dig as structural Verilog
module Template_04 (
  input  [6:0] In,
  output [6:0] Output
);

  wire and_1_out, and_2_out, and_3_out, and_4_out, and_5_out, and_6_out, and_7_out, C1, C2, C3, not_1_out,
       not_2_out, not_3_out;

  xor xor_1 (C1, In[3], In[2], In[1], In[0]);
  xor xor_2 (C2, In[4], In[5], In[1], In[0]);
  xor xor_3 (C3, In[6], In[4], In[2], In[0]);
  not not_1 (not_1_out, C1);
  not not_2 (not_2_out, C2);
  not not_3 (not_3_out, C3);
  and and_1 (and_1_out, not_1_out, not_2_out, C3);
  and and_2 (and_2_out, not_1_out, C2, not_3_out);
  and and_3 (and_3_out, not_1_out, C2, C3);
  and and_4 (and_4_out, C1, not_2_out, not_3_out);
  and and_5 (and_5_out, C1, not_2_out, C3);
  and and_6 (and_6_out, C1, C2, not_3_out);
  and and_7 (and_7_out, C1, C2, C3);
  xor xor_4 (Output[6], and_1_out, In[6]);
  xor xor_5 (Output[5], and_2_out, In[5]);
  xor xor_6 (Output[4], and_3_out, In[4]);
  xor xor_7 (Output[3], and_4_out, In[3]);
  xor xor_8 (Output[2], and_5_out, In[2]);
  xor xor_9 (Output[1], and_6_out, In[1]);
  xor xor_10 (Output[0], and_7_out, In[0]);

  // Other names for the same wires on the sheet: G = In[0]; F = In[1]; E = In[2]; D = In[3]; C = In[4]; B = In[5];
  //   A = In[6]
endmodule
