// Digital circuit Template-03.dig as structural Verilog
module Template_03 (
  input  [3:0] In,
  input  [1:0] Selector,
  output [3:0] Output
);

  wire and_1_out, and_2_out, and_3_out, and_4_out, and_5_out, and_6_out, and_7_out, and_10_out, and_11_out,
       and_12_out, and_13_out, and_16_out, and_17_out, and_18_out, and_19_out, and_20_out, and_21_out,
       and_24_out, and_25_out, and_26_out, and_27_out, and_28_out, and_29_out, and_30_out, not_1_out,
       not_2_out, not_4_out, not_5_out, not_6_out, not_7_out, not_8_out, not_9_out, not_10_out, not_11_out,
       not_12_out, not_13_out, not_14_out, not_15_out, not_16_out, not_17_out, not_18_out, not_19_out,
       not_20_out;
  wire [2:0] or_5_out;
  wire [3:0] E1, E2, E3, E4, or_1_out;
  wire [3:1] or_8_out, or_11_out;
  wire [3:3] and_8_out, and_14_out, and_22_out, and_31_out;

  not not_1 (not_1_out, In[2]);
  not not_2 (not_2_out, In[1]);
  not not_3 (or_1_out[0], In[0]);
  and and_1 (and_1_out, In[2], In[0]);
  and and_2 (and_2_out, In[2], In[1]);
  and and_3 (and_3_out, not_1_out, In[0]);
  and and_4 (and_4_out, not_1_out, In[1]);
  and and_5 (and_5_out, In[2], not_2_out, or_1_out[0]);
  and and_6 (and_6_out, not_2_out, or_1_out[0]);
  and and_7 (and_7_out, In[1], In[0]);
  or or_1 (or_1_out[3], In[3], and_1_out, and_2_out);
  or or_2 (or_1_out[2], and_3_out, and_4_out, and_5_out);
  or or_3 (or_1_out[1], and_6_out, and_7_out);
  not not_4 (not_4_out, Selector[1]);
  not not_5 (not_5_out, Selector[0]);
  and and_8 (and_8_out[3], not_4_out, not_5_out);
  assign E1 = or_1_out & {4{and_8_out[3]}};  // And and_9, 4 bits wide
  not not_6 (not_6_out, In[2]);
  not not_7 (not_7_out, In[1]);
  not not_8 (not_8_out, In[0]);
  or or_4 (or_5_out[2], In[3], In[2]);
  and and_10 (and_10_out, not_6_out, In[1]);
  and and_11 (and_11_out, In[2], not_7_out);
  and and_12 (and_12_out, not_7_out, In[0]);
  and and_13 (and_13_out, In[1], not_8_out);
  or or_5 (or_5_out[1], and_10_out, and_11_out);
  or or_6 (or_5_out[0], and_12_out, and_13_out);
  not not_9 (not_9_out, Selector[1]);
  not not_10 (not_10_out, Selector[0]);
  assign Output = E1 | E2 | E3 | E4;  // Or or_7, 4 bits wide
  and and_14 (and_14_out[3], not_9_out, Selector[0]);
  assign E2 = {In[3], or_5_out} & {4{and_14_out[3]}};  // And and_15, 4 bits wide
  not not_11 (not_11_out, In[2]);
  not not_12 (not_12_out, In[1]);
  not not_13 (not_13_out, In[0]);
  and and_16 (and_16_out, In[2], In[0]);
  and and_17 (and_17_out, In[2], In[1]);
  and and_18 (and_18_out, In[2], not_13_out);
  and and_19 (and_19_out, In[2], In[1]);
  and and_20 (and_20_out, not_11_out, In[1]);
  and and_21 (and_21_out, In[2], not_12_out, In[0]);
  or or_8 (or_8_out[3], In[3], and_16_out, and_17_out);
  or or_9 (or_8_out[2], In[3], and_18_out, and_19_out);
  or or_10 (or_8_out[1], In[3], and_20_out, and_21_out);
  not not_14 (not_14_out, Selector[1]);
  not not_15 (not_15_out, Selector[0]);
  and and_22 (and_22_out[3], Selector[1], not_15_out);
  assign E3 = {or_8_out, In[0]} & {4{and_22_out[3]}};  // And and_23, 4 bits wide
  not not_16 (not_16_out, In[2]);
  not not_17 (not_17_out, In[1]);
  not not_18 (not_18_out, In[0]);
  and and_24 (and_24_out, In[2], In[0]);
  and and_25 (and_25_out, In[1], In[0]);
  and and_26 (and_26_out, not_16_out, not_17_out, In[0]);
  and and_27 (and_27_out, In[2], not_18_out);
  and and_28 (and_28_out, In[2], In[1]);
  and and_29 (and_29_out, In[2], not_17_out, In[0]);
  and and_30 (and_30_out, In[1], not_18_out);
  not not_19 (not_19_out, Selector[1]);
  or or_11 (or_11_out[3], In[3], and_24_out, and_25_out);
  or or_12 (or_11_out[2], and_26_out, and_27_out, and_28_out);
  or or_13 (or_11_out[1], In[3], and_29_out, and_30_out);
  not not_20 (not_20_out, Selector[0]);
  and and_31 (and_31_out[3], Selector[1], Selector[0]);
  assign E4 = {or_11_out, In[0]} & {4{and_31_out[3]}};  // And and_32, 4 bits wide

  // Other names for the same wires on the sheet: D = In[0]; C = In[1]; B = In[2]; A = In[3]; S[1:0] = Selector
endmodule
