// Digital circuit Full adder.dig as structural Verilog
module Full_adder (
  input  A,
  input  B,
  input  B_2,
  output Sum,
  output Cout
);

  wire _7400_1_pin3, _7400_1_pin6, _7400_1_pin8, _7400_1_pin10, _7400_2_pin3, _7400_2_pin6, _7400_2_pin10;

  _7400 _7400_1 (
    .pin1(A), .pin2(B), .pin3(_7400_1_pin3), .pin4(_7400_1_pin3), .pin5(B), .pin6(_7400_1_pin6), .pin7(1'b0),
    .pin8(_7400_1_pin8), .pin9(_7400_1_pin6), .pin10(_7400_1_pin10), .pin11(_7400_1_pin10),
    .pin12(_7400_1_pin3), .pin13(A), .pin14(1'b1));
  _7400 _7400_2 (
    .pin1(_7400_1_pin8), .pin2(B_2), .pin3(_7400_2_pin3), .pin4(_7400_2_pin3), .pin5(B_2),
    .pin6(_7400_2_pin6), .pin7(1'b0), .pin8(Sum), .pin9(_7400_2_pin6), .pin10(_7400_2_pin10),
    .pin11(_7400_2_pin10), .pin12(_7400_2_pin3), .pin13(_7400_1_pin8), .pin14(1'b1));
  _7400 _7400_3 (
    .pin1(_7400_2_pin3), .pin2(_7400_1_pin3), .pin3(Cout), .pin4(1'b0), .pin5(1'b0), .pin7(1'b0),
    .pin9(1'b0), .pin10(1'b0), .pin12(1'b0), .pin13(1'b0), .pin14(1'b1));  // open: pin6, pin8, pin11

  // Other names for the same wires on the sheet: C = B_2
endmodule
