// Digital circuit 1-bit Logical.dig as structural Verilog
module _1_bit_Logical (
  input  A,
  input  B,
  input  [2:0] S,
  output Out
);

  wire and_1_out, nand_1_out, nor_1_out, not_1_out, not_2_out, not_3_out, xnor_1_out;

  not not_1 (not_1_out, A);
  nand nand_1 (nand_1_out, A, B);
  nor nor_1 (nor_1_out, A, B);
  xnor xnor_1 (xnor_1_out, A, B);
  and and_1 (and_1_out, A, ~B);  // And
  Multiplexer #(.Selector_Bits(3)) multiplexer_1 (
    .sel(S), .in_0(not_1_out), .in_1(nand_1_out), .in_2(nor_1_out), .in_3(xnor_1_out), .in_4(not_2_out),
    .in_5(not_3_out), .in_6(and_1_out), .in_7(A), .out(Out));
  not not_2 (not_2_out, nand_1_out);
  not not_3 (not_3_out, nor_1_out);
  // Pins of 1 and 3 bits meet at S
endmodule
