// Digital circuit Template.dig as structural Verilog
module Template (
  input  [3:0] A,
  input  [3:0] B,
  input  [2:0] S,
  input  M,
  input  C,
  output [3:0] F,
  output Cout
);

  wire _1_bit_logical_1_p4, _1_bit_logical_2_p3, _1_bit_logical_3_p3, _1_bit_logical_4_p3, add_2_c_o,
       add_3_s, and_1_out, and_2_out, and_3_out, and_4_out, C0, C1, C2, C3, multiplexer_6_out, nand_1_out,
       nand_2_out, nand_3_out, nand_4_out, nor_1_out, nor_2_out, nor_3_out, nor_4_out, not_1_out, not_2_out,
       not_3_out, not_4_out, not_5_out, not_6_out, not_7_out, not_8_out, not_9_out, not_10_out, not_11_out,
       not_12_out, xnor_1_out, xnor_2_out, xnor_3_out, xnor_4_out;
  wire [3:0] add_1_s, add_2_s, barrelshifter_1_out, barrelshifter_2_out, multiplexer_4_out,
       multiplexer_5_out, neg_1_out, sub_1_s, sub_2_s, sub_3_s;

  not not_1 (not_1_out, A[0]);
  nand nand_1 (nand_1_out, A[0], B[0]);
  nor nor_1 (nor_1_out, A[0], B[0]);
  xnor xnor_1 (xnor_1_out, A[0], B[0]);
  and and_1 (and_1_out, A[0], ~B[0]);  // And
  not not_2 (not_2_out, A[1]);
  nand nand_2 (nand_2_out, A[1], B[1]);
  nor nor_2 (nor_2_out, A[1], B[1]);
  xnor xnor_2 (xnor_2_out, A[1], B[1]);
  and and_2 (and_2_out, A[1], ~B[1]);  // And
  not not_3 (not_3_out, A[2]);
  nand nand_3 (nand_3_out, A[2], B[2]);
  nor nor_3 (nor_3_out, A[2], B[2]);
  xnor xnor_3 (xnor_3_out, A[2], B[2]);
  and and_3 (and_3_out, A[2], ~B[2]);  // And
  not not_4 (not_4_out, A[3]);
  nand nand_4 (nand_4_out, A[3], B[3]);
  nor nor_4 (nor_4_out, A[3], B[3]);
  xnor xnor_4 (xnor_4_out, A[3], B[3]);
  and and_4 (and_4_out, A[3], ~B[3]);  // And
  not not_5 (not_5_out, nand_1_out);
  not not_6 (not_6_out, nor_1_out);
  not not_7 (not_7_out, nand_2_out);
  not not_8 (not_8_out, nor_2_out);
  not not_9 (not_9_out, nand_3_out);
  not not_10 (not_10_out, nor_3_out);
  not not_11 (not_11_out, nand_4_out);
  not not_12 (not_12_out, nor_4_out);
  Multiplexer #(.Selector_Bits(3)) multiplexer_1 (
    .sel(S), .in_0(not_1_out), .in_1(nand_1_out), .in_2(nor_1_out), .in_3(xnor_1_out), .in_4(not_5_out),
    .in_5(not_6_out), .in_6(and_1_out), .in_7(A[0]), .out(multiplexer_4_out[0]));
  Multiplexer #(.Selector_Bits(3)) multiplexer_2 (
    .sel(S), .in_0(not_2_out), .in_1(nand_2_out), .in_2(nor_2_out), .in_3(xnor_2_out), .in_4(not_7_out),
    .in_5(not_8_out), .in_6(and_2_out), .in_7(A[1]), .out(multiplexer_4_out[1]));
  Multiplexer #(.Selector_Bits(3)) multiplexer_3 (
    .sel(S), .in_0(not_3_out), .in_1(nand_3_out), .in_2(nor_3_out), .in_3(xnor_3_out), .in_4(not_9_out),
    .in_5(not_10_out), .in_6(and_3_out), .in_7(A[2]), .out(multiplexer_4_out[2]));
  Multiplexer #(.Selector_Bits(3)) multiplexer_4 (
    .sel(S), .in_0(not_4_out), .in_1(nand_4_out), .in_2(nor_4_out), .in_3(xnor_4_out), .in_4(not_11_out),
    .in_5(not_12_out), .in_6(and_4_out), .in_7(A[3]), .out(multiplexer_4_out[3]));
  Neg #(.Bits(4)) neg_1 (.in(A), .out(neg_1_out));
  Sub #(.Bits(4)) sub_1 (.a(A), .b(4'b0001), .c_i(1'b0), .s(sub_1_s), .c_o(C1));
  Add #(.Bits(4)) add_1 (.a(A), .b(B), .c_i(1'b0), .s(add_1_s), .c_o(C2));
  Sub #(.Bits(4)) sub_2 (.a(A), .b(B), .c_i(1'b1), .s(sub_2_s), .c_o(C3));
  Sub #(.Bits(4)) sub_3 (.a(neg_1_out), .b(4'b0001), .c_i(1'b0), .s(sub_3_s), .c_o(C0));
  BarrelShifter #(.Bits(4)) barrelshifter_1 (.in(A), .shift(3'b001), .out(barrelshifter_1_out));
  BarrelShifter #(.Bits(4), .direction("right")) barrelshifter_2 (.in(A), .shift(3'b001), .out(barrelshifter_2_out));
  Multiplexer #(.Bits(4), .Selector_Bits(3)) multiplexer_5 (
    .sel(S), .in_0(A), .in_1(sub_1_s), .in_2(add_1_s), .in_3(sub_2_s), .in_4(sub_3_s), .in_5(B),
    .in_6(barrelshifter_1_out), .in_7(barrelshifter_2_out), .out(multiplexer_5_out));
  // _1_bit_Logical _1_bit_logical_1: pin names not known; wires that end beside it: S, S, B[3], _1_bit_logical_1_p4, A[3]
  Add #(.Bits(4)) add_2 (.a(multiplexer_5_out), .b({3'b000, C}), .c_i(1'b0), .s(add_2_s), .c_o(add_2_c_o));
  Multiplexer #(.Selector_Bits(3)) multiplexer_6 (
    .sel(S), .in_0(1'b0), .in_1(C0), .in_2(C1), .in_3(C2), .in_4(C3), .in_5(1'b0), .in_6(1'b0), .in_7(1'b0),
    .out(multiplexer_6_out));
  // _1_bit_Logical _1_bit_logical_2: pin names not known; wires that end beside it: S, B[2], _1_bit_logical_2_p3, A[2]
  // _1_bit_Logical _1_bit_logical_3: pin names not known; wires that end beside it: S, B[1], _1_bit_logical_3_p3, A[1]
  Multiplexer #(.Bits(4)) multiplexer_7 (.sel(M), .in_0(multiplexer_4_out), .in_1(add_2_s), .out(F));
  // _1_bit_Logical _1_bit_logical_4: pin names not known; wires that end beside it: S, B[0], _1_bit_logical_4_p3, A[0]
  Add add_3 (.a(add_2_c_o), .b(multiplexer_6_out), .c_i(1'b0), .s(add_3_s));  // open: c_o
  and and_5 (Cout, add_3_s, M);
endmodule
