// Digital circuit Template.dig as structural Verilog
module Template (
  input  A,
  input  B,
  input  Clock,
  input  Clr,
  output Z
);

  wire add_1_c_o, add_1_s, and_2_out, d_ff_1_q;

  Add add_1 (.a(A), .b(B), .c_i(d_ff_1_q), .s(add_1_s), .c_o(add_1_c_o));
  and and_1 (Z, Clr, add_1_s);
  and and_2 (and_2_out, add_1_c_o, Clr);
  D_FF d_ff_1 (.D(and_2_out), .C(Clock), .Q(d_ff_1_q));  // open: nQ
endmodule
