// Digital circuit Template.dig as structural Verilog
module Template (
  input  P5,
  input  reset,
  input  clock,
  input  P10,
  input  P20,
  input  Pcoffee,
  input  Ptea,
  input  Pchange,
  input  Pnext,
  output [5:0] Balance,
  output CoffeeOut,
  output TeaOut,
  output [1:0] Change5,
  output [1:0] Change10,
  output [1:0] Change20
);

  wire Add_enb, and_12_out, and_13_out, and_14_out, and_19_out, and_20_out, Buy_enb, comparator_1_eq,
       comparator_1_gt, comparator_1_lt, comparator_2_eq, comparator_2_gt, comparator_2_lt, comparator_3_eq,
       comparator_3_gt, comparator_3_lt, comparator_4_gt, comparator_5_gt, comparator_6_gt, comparator_7_lt,
       comparator_8_lt, d_ff_1_q, d_ff_2_q, d_ff_3_q, d_ff_4_q, d_ff_5_q, d_ff_6_q, d_ff_7_q, d_ff_8_q,
       d_ff_9_q, d_ff_10_q, d_ff_11_q, d_ff_12_q, d_ff_13_q, d_ff_14_q, d_ff_15_q, d_ff_16_q, not_1_out,
       not_2_out, not_3_out, not_4_out, not_5_out, not_6_out, not_7_out, not_8_out, or_1_out, or_2_out,
       or_3_out, or_4_out, or_5_out, or_6_out, or_8_out, or_9_out, P_5, P_10, P_20, P_change, P_coffee,
       P_next, P_tea, reset_t, Sub_5, Sub_10, Sub_20, Sub_enb, xor_1_out, xor_2_out, xor_3_out, xor_4_out,
       xor_5_out, xor_6_out;
  wire [1:0] and_16_out, and_18_out, and_23_out;
  wire [5:0] add_1_s, multiplexer_1_out, multiplexer_2_out, multiplexer_3_out, multiplexer_4_out, sub_1_s,
       sub_2_s;

  D_FF d_ff_1 (.D(P5), .C(clock), .Q(d_ff_1_q));  // open: nQ
  D_FF d_ff_2 (.D(P10), .C(clock), .Q(d_ff_2_q));  // open: nQ
  D_FF d_ff_3 (.D(P20), .C(clock), .Q(d_ff_3_q));  // open: nQ
  D_FF d_ff_4 (.D(Ptea), .C(clock), .Q(d_ff_4_q));  // open: nQ
  D_FF d_ff_5 (.D(Pcoffee), .C(clock), .Q(d_ff_5_q));  // open: nQ
  D_FF d_ff_6 (.D(Pchange), .C(clock), .Q(d_ff_6_q));  // open: nQ
  D_FF d_ff_7 (.D(Pnext), .C(clock), .Q(d_ff_7_q));  // open: nQ
  D_FF d_ff_8 (.D(reset), .C(clock), .Q(d_ff_8_q));  // open: nQ
  D_FF d_ff_9 (.D(d_ff_1_q), .C(clock), .Q(d_ff_9_q));  // open: nQ
  D_FF d_ff_10 (.D(d_ff_2_q), .C(clock), .Q(d_ff_10_q));  // open: nQ
  D_FF d_ff_11 (.D(d_ff_3_q), .C(clock), .Q(d_ff_11_q));  // open: nQ
  D_FF d_ff_12 (.D(d_ff_4_q), .C(clock), .Q(d_ff_12_q));  // open: nQ
  D_FF d_ff_13 (.D(d_ff_5_q), .C(clock), .Q(d_ff_13_q));  // open: nQ
  D_FF d_ff_14 (.D(d_ff_6_q), .C(clock), .Q(d_ff_14_q));  // open: nQ
  D_FF d_ff_15 (.D(d_ff_7_q), .C(clock), .Q(d_ff_15_q));  // open: nQ
  D_FF d_ff_16 (.D(d_ff_8_q), .C(clock), .Q(d_ff_16_q));  // open: nQ
  not not_1 (not_1_out, d_ff_9_q);
  not not_2 (not_2_out, d_ff_10_q);
  not not_3 (not_3_out, d_ff_11_q);
  not not_4 (not_4_out, d_ff_12_q);
  not not_5 (not_5_out, d_ff_13_q);
  not not_6 (not_6_out, d_ff_14_q);
  not not_7 (not_7_out, d_ff_15_q);
  not not_8 (not_8_out, d_ff_16_q);
  or or_1 (or_1_out, P_change, or_2_out);
  and and_1 (P_5, d_ff_1_q, not_1_out);
  and and_2 (P_10, d_ff_2_q, not_2_out);
  and and_3 (P_20, d_ff_3_q, not_3_out);
  and and_4 (P_tea, d_ff_4_q, not_4_out);
  and and_5 (P_coffee, d_ff_5_q, not_5_out);
  and and_6 (P_change, d_ff_6_q, not_6_out);
  and and_7 (P_next, d_ff_7_q, not_7_out);
  and and_8 (reset_t, d_ff_8_q, not_8_out);
  Register register_1 (.D(P_change), .C(clock), .en(or_1_out), .Q(Sub_enb));
  Comparator #(.Bits(6)) comparator_1 (
    .a(Balance), .b(6'b010100), .gt(comparator_1_gt), .eq(comparator_1_eq), .lt(comparator_1_lt));
  Comparator #(.Bits(6)) comparator_2 (
    .a(Balance), .b(6'b001010), .gt(comparator_2_gt), .eq(comparator_2_eq), .lt(comparator_2_lt));
  Comparator #(.Bits(6)) comparator_3 (
    .a(Balance), .b({6{1'b0}}), .gt(comparator_3_gt), .eq(comparator_3_eq), .lt(comparator_3_lt));
  or or_2 (or_2_out, comparator_3_eq, comparator_3_lt);
  or or_3 (or_3_out, comparator_1_gt, comparator_1_eq);
  or or_4 (or_4_out, comparator_2_gt, comparator_2_eq);
  and and_9 (Sub_20, Sub_enb, or_3_out);
  and and_10 (Sub_10, comparator_1_lt, Sub_enb, or_4_out);
  and and_11 (Sub_5, comparator_2_lt, Sub_enb, comparator_3_gt);
  or or_5 (or_5_out, reset_t, P_change);
  Counter #(.Bits(2)) counter_1 (.en(Sub_20), .C(clock), .clr(or_5_out), .out(Change20));  // open: ovf
  Counter #(.Bits(2)) counter_2 (.en(Sub_10), .C(clock), .clr(or_5_out), .out(Change10));  // open: ovf
  Counter #(.Bits(2)) counter_3 (.en(Sub_5), .C(clock), .clr(or_5_out), .out(Change5));  // open: ovf
  xor xor_1 (xor_1_out, P_20, P_10);
  xor xor_2 (xor_2_out, P_5, P_20);
  xor xor_3 (xor_3_out, Sub_20, Sub_10);
  xor xor_4 (xor_4_out, Sub_5, Sub_20);
  Comparator #(.Bits(6)) comparator_4 (.a(Balance), .b(6'b101101), .gt(comparator_4_gt));  // open: eq, lt
  Comparator #(.Bits(6)) comparator_5 (.a(Balance), .b(6'b101000), .gt(comparator_5_gt));  // open: eq, lt
  Comparator #(.Bits(6)) comparator_6 (.a(Balance), .b(6'b011110), .gt(comparator_6_gt));  // open: eq, lt
  Comparator #(.Bits(6)) comparator_7 (.a(Balance), .b(6'b010100), .lt(comparator_7_lt));  // open: gt, eq
  Comparator #(.Bits(6)) comparator_8 (.a(Balance), .b(6'b011001), .lt(comparator_8_lt));  // open: gt, eq
  and and_12 (and_12_out, ~comparator_4_gt, P_5);  // And
  and and_13 (and_13_out, ~comparator_5_gt, P_10);  // And
  and and_14 (and_14_out, ~comparator_6_gt, P_20);  // And
  and and_15 (and_16_out[1], xor_1_out, ~P_5);  // And
  and and_16 (and_16_out[0], xor_2_out, ~P_10);  // And
  and and_17 (and_18_out[1], xor_3_out, ~Sub_5);  // And
  and and_18 (and_18_out[0], xor_4_out, ~Sub_10);  // And
  and and_19 (and_19_out, P_tea, ~TeaOut, ~comparator_7_lt);  // And
  and and_20 (and_20_out, P_coffee, ~CoffeeOut, ~comparator_8_lt);  // And
  or or_6 (or_6_out, and_12_out, and_13_out, and_14_out);
  Multiplexer #(.Selector_Bits(2), .Bits(6)) multiplexer_1 (
    .sel(and_16_out), .in_0({6{1'b0}}), .in_1(6'b000101), .in_2(6'b001010), .in_3(6'b010100),
    .out(multiplexer_1_out));
  Multiplexer #(.Selector_Bits(2), .Bits(6)) multiplexer_2 (
    .sel(and_18_out), .in_0({6{1'b0}}), .in_1(6'b000101), .in_2(6'b001010), .in_3(6'b010100),
    .out(multiplexer_2_out));
  Multiplexer #(.Selector_Bits(2), .Bits(6)) multiplexer_3 (
    .sel({P_coffee, P_tea}), .in_0({6{1'b0}}), .in_1(6'b010100), .in_2(6'b011001), .in_3({6{1'b0}}),
    .out(multiplexer_3_out));
  or or_7 (Buy_enb, and_19_out, and_20_out);
  xor xor_5 (xor_5_out, Buy_enb, Sub_enb);
  xor xor_6 (xor_6_out, Add_enb, Buy_enb);
  and and_21 (Add_enb, or_6_out, ~TeaOut, ~CoffeeOut);  // And
  or or_8 (or_8_out, Buy_enb, P_change, P_next, reset_t);
  Add #(.Bits(6)) add_1 (.a(Balance), .b(multiplexer_1_out), .c_i(1'b0), .s(add_1_s));  // open: c_o
  Sub #(.Bits(6)) sub_1 (.a(Balance), .b(multiplexer_2_out), .c_i(1'b0), .s(sub_1_s));  // open: c_o
  Sub #(.Bits(6)) sub_2 (.a(Balance), .b(multiplexer_3_out), .c_i(1'b0), .s(sub_2_s));  // open: c_o
  and and_22 (and_23_out[1], xor_5_out, ~Add_enb);  // And
  and and_23 (and_23_out[0], xor_6_out, ~Sub_enb);  // And
  Multiplexer #(.Selector_Bits(2), .Bits(6)) multiplexer_4 (
    .sel(and_23_out), .in_0({6{1'b0}}), .in_1(add_1_s), .in_2(sub_1_s), .in_3(sub_2_s),
    .out(multiplexer_4_out));
  Register register_2 (.D(and_19_out), .C(clock), .en(or_8_out), .Q(TeaOut));
  Register register_3 (.D(and_20_out), .C(clock), .en(or_8_out), .Q(CoffeeOut));
  or or_9 (or_9_out, Add_enb, Sub_enb, Buy_enb, reset_t);
  Register #(.Bits(6)) register_4 (.D(multiplexer_4_out), .C(clock), .en(or_9_out), .Q(Balance));

  // Other names for the same wires on the sheet: Change_5[1:0] = Change5; Change_10[1:0] = Change10;
  //   Change_20[1:0] = Change20; clk = clock

  // Notes on the sheet:
  //   Changes
  //   Add Balance
  //   Buy
  //   Edit Balance
endmodule

/* Test case T1:
clock reset P5 P10 P20 Pcoffee Ptea Pchange Pnext Balance CoffeeOut TeaOut Change5 Change10 Change20
0 1 0 0 0 0 0 0 0 x x x x x x
1 1 0 0 0 0 0 0 0 0 0 0 0 0 0
0 0 1 0 0 0 0 0 0 0 0 0 0 0 0
1 0 1 0 0 0 0 0 0 0 0 0 0 0 0
0 0 0 0 0 0 0 0 0 x x x x x x
1 0 0 0 0 0 0 0 0 x x x x x x
0 0 0 0 0 0 0 0 0 x x x x x x
1 0 0 0 0 0 0 0 0 x x x x x x
0 0 0 0 0 0 0 0 0 x x x x x x
1 0 0 0 0 0 0 0 0 x x x x x x
0 0 0 0 0 0 0 0 0 x x x x x x
1 0 0 0 0 0 0 0 0 x x x x x x
0 0 0 0 0 0 0 0 0 x x x x x x
1 0 0 0 0 0 0 0 0 x x x x x x
0 0 0 0 0 0 0 0 0 x x x x x x
1 0 0 0 0 0 0 0 0 x x x x x x
0 0 0 0 0 0 0 0 0 x x x x x x
1 0 0 0 0 0 0 0 0 x x x x x x
0 0 0 0 0 0 0 0 0 x x x x x x
1 0 0 0 0 0 0 0 0 x x x x x x
0 0 0 0 0 0 0 0 0 x x x x x x
1 0 0 0 0 0 0 0 0 x x x x x x
0 0 0 0 0 0 0 0 0 x x x x x x
1 0 0 0 0 0 0 0 0 x x x x x x
0 0 0 0 0 0 0 0 0 x x x x x x
1 0 0 0 0 0 0 0 0 x x x x x x
0 0 0 0 0 0 0 0 0 x x x x x x
1 0 0 0 0 0 0 0 0 x x x x x x
0 0 0 0 0 0 0 0 0 x x x x x x
1 0 0 0 0 0 0 0 0 x x x x x x
0 0 0 0 0 0 0 0 0 x x x x x x
1 0 0 0 0 0 0 0 0 x x x x x x
0 0 0 0 0 0 0 0 0 x x x x x x
1 0 0 0 0 0 0 0 0 x x x x x x
0 0 0 0 0 0 0 0 0 x x x x x x
1 0 0 0 0 0 0 0 0 x x x x x x
0 0 0 0 0 0 0 0 0 x x x x x x
1 0 0 0 0 0 0 0 0 x x x x x x
0 0 0 0 0 0 0 0 0 x x x x x x
1 0 0 0 0 0 0 0 0 x x x x x x
0 0 0 0 0 0 0 0 0 x x x x x x
1 0 0 0 0 0 0 0 0 x x x x x x
0 0 0 0 0 0 0 0 0 x x x x x x
1 0 0 0 0 0 0 0 0 x x x x x x
0 0 0 0 0 0 0 0 0 5 0 0 0 0 0
1 0 0 0 0 0 0 0 0 5 0 0 0 0 0
0 0 0 1 0 0 0 0 0 5 0 0 0 0 0
1 0 0 1 0 0 0 0 0 5 0 0 0 0 0
0 0 0 0 0 0 0 0 0 x x x x x x
1 0 0 0 0 0 0 0 0 x x x x x x
0 0 0 0 0 0 0 0 0 x x x x x x
1 0 0 0 0 0 0 0 0 x x x x x x
0 0 0 0 0 0 0 0 0 x x x x x x
1 0 0 0 0 0 0 0 0 x x x x x x
0 0 0 0 0 0 0 0 0 x x x x x x
1 0 0 0 0 0 0 0 0 x x x x x x
0 0 0 0 0 0 0 0 0 x x x x x x
1 0 0 0 0 0 0 0 0 x x x x x x
0 0 0 0 0 0 0 0 0 x x x x x x
1 0 0 0 0 0 0 0 0 x x x x x x
0 0 0 0 0 0 0 0 0 x x x x x x
1 0 0 0 0 0 0 0 0 x x x x x x
0 0 0 0 0 0 0 0 0 x x x x x x
1 0 0 0 0 0 0 0 0 x x x x x x
0 0 0 0 0 0 0 0 0 x x x x x x
1 0 0 0 0 0 0 0 0 x x x x x x
0 0 0 0 0 0 0 0 0 x x x x x x
1 0 0 0 0 0 0 0 0 x x x x x x
0 0 0 0 0 0 0 0 0 x x x x x x
1 0 0 0 0 0 0 0 0 x x x x x x
0 0 0 0 0 0 0 0 0 x x x x x x
1 0 0 0 0 0 0 0 0 x x x x x x
0 0 0 0 0 0 0 0 0 x x x x x x
1 0 0 0 0 0 0 0 0 x x x x x x
0 0 0 0 0 0 0 0 0 x x x x x x
1 0 0 0 0 0 0 0 0 x x x x x x
0 0 0 0 0 0 0 0 0 x x x x x x
1 0 0 0 0 0 0 0 0 x x x x x x
0 0 0 0 0 0 0 0 0 x x x x x x
1 0 0 0 0 0 0 0 0 x x x x x x
0 0 0 0 0 0 0 0 0 x x x x x x
1 0 0 0 0 0 0 0 0 x x x x x x
0 0 0 0 0 0 0 0 0 x x x x x x
1 0 0 0 0 0 0 0 0 x x x x x x
0 0 0 0 0 0 0 0 0 x x x x x x
1 0 0 0 0 0 0 0 0 x x x x x x
0 0 0 0 0 0 0 0 0 x x x x x x
1 0 0 0 0 0 0 0 0 x x x x x x
0 0 0 0 0 0 0 0 0 15 0 0 0 0 0
1 0 0 0 0 0 0 0 0 15 0 0 0 0 0
0 0 0 0 1 0 0 0 0 15 0 0 0 0 0
1 0 0 0 1 0 0 0 0 15 0 0 0 0 0
0 0 0 0 0 0 0 0 0 x x x x x x
1 0 0 0 0 0 0 0 0 x x x x x x
0 0 0 0 0 0 0 0 0 x x x x x x
1 0 0 0 0 0 0 0 0 x x x x x x
0 0 0 0 0 0 0 0 0 x x x x x x
1 0 0 0 0 0 0 0 0 x x x x x x
0 0 0 0 0 0 0 0 0 x x x x x x
1 0 0 0 0 0 0 0 0 x x x x x x
0 0 0 0 0 0 0 0 0 x x x x x x
1 0 0 0 0 0 0 0 0 x x x x x x
0 0 0 0 0 0 0 0 0 x x x x x x
1 0 0 0 0 0 0 0 0 x x x x x x
0 0 0 0 0 0 0 0 0 x x x x x x
1 0 0 0 0 0 0 0 0 x x x x x x
0 0 0 0 0 0 0 0 0 x x x x x x
1 0 0 0 0 0 0 0 0 x x x x x x
0 0 0 0 0 0 0 0 0 x x x x x x
1 0 0 0 0 0 0 0 0 x x x x x x
0 0 0 0 0 0 0 0 0 x x x x x x
1 0 0 0 0 0 0 0 0 x x x x x x
0 0 0 0 0 0 0 0 0 x x x x x x
1 0 0 0 0 0 0 0 0 x x x x x x
0 0 0 0 0 0 0 0 0 x x x x x x
1 0 0 0 0 0 0 0 0 x x x x x x
0 0 0 0 0 0 0 0 0 x x x x x x
1 0 0 0 0 0 0 0 0 x x x x x x
0 0 0 0 0 0 0 0 0 x x x x x x
1 0 0 0 0 0 0 0 0 x x x x x x
0 0 0 0 0 0 0 0 0 x x x x x x
1 0 0 0 0 0 0 0 0 x x x x x x
0 0 0 0 0 0 0 0 0 x x x x x x
1 0 0 0 0 0 0 0 0 x x x x x x
0 0 0 0 0 0 0 0 0 x x x x x x
1 0 0 0 0 0 0 0 0 x x x x x x
0 0 0 0 0 0 0 0 0 x x x x x x
1 0 0 0 0 0 0 0 0 x x x x x x
0 0 0 0 0 0 0 0 0 x x x x x x
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*/

/* Test case T2:
clock reset P5 P10 P20 Pcoffee Ptea Pchange Pnext Balance CoffeeOut TeaOut Change5 Change10 Change20
0 1 0 0 0 0 0 0 0 x x x x x x
1 1 0 0 0 0 0 0 0 0 0 0 0 0 0
0 0 0 0 0 1 0 0 0 0 0 0 0 0 0
1 0 0 0 0 1 0 0 0 0 0 0 0 0 0
0 0 0 0 0 0 0 0 0 x x x x x x
1 0 0 0 0 0 0 0 0 x x x x x x
0 0 0 0 0 0 0 0 0 x x x x x x
1 0 0 0 0 0 0 0 0 x x x x x x
0 0 0 0 0 0 0 0 0 x x x x x x
1 0 0 0 0 0 0 0 0 x x x x x x
0 0 0 0 0 0 0 0 0 x x x x x x
1 0 0 0 0 0 0 0 0 x x x x x x
0 0 0 0 0 0 0 0 0 x x x x x x
1 0 0 0 0 0 0 0 0 x x x x x x
0 0 0 0 0 0 0 0 0 x x x x x x
1 0 0 0 0 0 0 0 0 x x x x x x
0 0 0 0 0 0 0 0 0 x x x x x x
1 0 0 0 0 0 0 0 0 x x x x x x
0 0 0 0 0 0 0 0 0 x x x x x x
1 0 0 0 0 0 0 0 0 x x x x x x
0 0 0 0 0 0 0 0 0 x x x x x x
1 0 0 0 0 0 0 0 0 x x x x x x
0 0 0 0 0 0 0 0 0 x x x x x x
1 0 0 0 0 0 0 0 0 x x x x x x
0 0 0 0 0 0 0 0 0 x x x x x x
1 0 0 0 0 0 0 0 0 x x x x x x
0 0 0 0 0 0 0 0 0 x x x x x x
1 0 0 0 0 0 0 0 0 x x x x x x
0 0 0 0 0 0 0 0 0 x x x x x x
1 0 0 0 0 0 0 0 0 x x x x x x
0 0 0 0 0 0 0 0 0 x x x x x x
1 0 0 0 0 0 0 0 0 x x x x x x
0 0 0 0 0 0 0 0 0 x x x x x x
1 0 0 0 0 0 0 0 0 x x x x x x
0 0 0 0 0 0 0 0 0 x x x x x x
1 0 0 0 0 0 0 0 0 x x x x x x
0 0 0 0 0 0 0 0 0 x x x x x x
1 0 0 0 0 0 0 0 0 x x x x x x
0 0 0 0 0 0 0 0 0 x x x x x x
1 0 0 0 0 0 0 0 0 x x x x x x
0 0 0 0 0 0 0 0 0 x x x x x x
1 0 0 0 0 0 0 0 0 x x x x x x
0 0 0 0 0 0 0 0 0 x x x x x x
1 0 0 0 0 0 0 0 0 x x x x x x
0 0 0 0 0 0 0 0 0 0 0 0 0 0 0
1 0 0 0 0 0 0 0 0 0 0 0 0 0 0
0 0 0 0 0 0 1 0 0 0 0 0 0 0 0
1 0 0 0 0 0 1 0 0 0 0 0 0 0 0
0 0 0 0 0 0 0 0 0 x x x x x x
1 0 0 0 0 0 0 0 0 x x x x x x
0 0 0 0 0 0 0 0 0 x x x x x x
1 0 0 0 0 0 0 0 0 x x x x x x
0 0 0 0 0 0 0 0 0 x x x x x x
1 0 0 0 0 0 0 0 0 x x x x x x
0 0 0 0 0 0 0 0 0 x x x x x x
1 0 0 0 0 0 0 0 0 x x x x x x
0 0 0 0 0 0 0 0 0 x x x x x x
1 0 0 0 0 0 0 0 0 x x x x x x
0 0 0 0 0 0 0 0 0 x x x x x x
1 0 0 0 0 0 0 0 0 x x x x x x
0 0 0 0 0 0 0 0 0 x x x x x x
1 0 0 0 0 0 0 0 0 x x x x x x
0 0 0 0 0 0 0 0 0 x x x x x x
1 0 0 0 0 0 0 0 0 x x x x x x
0 0 0 0 0 0 0 0 0 x x x x x x
1 0 0 0 0 0 0 0 0 x x x x x x
0 0 0 0 0 0 0 0 0 x x x x x x
1 0 0 0 0 0 0 0 0 x x x x x x
0 0 0 0 0 0 0 0 0 x x x x x x
1 0 0 0 0 0 0 0 0 x x x x x x
0 0 0 0 0 0 0 0 0 x x x x x x
1 0 0 0 0 0 0 0 0 x x x x x x
0 0 0 0 0 0 0 0 0 x x x x x x
1 0 0 0 0 0 0 0 0 x x x x x x
0 0 0 0 0 0 0 0 0 x x x x x x
1 0 0 0 0 0 0 0 0 x x x x x x
0 0 0 0 0 0 0 0 0 x x x x x x
1 0 0 0 0 0 0 0 0 x x x x x x
0 0 0 0 0 0 0 0 0 x x x x x x
1 0 0 0 0 0 0 0 0 x x x x x x
0 0 0 0 0 0 0 0 0 x x x x x x
1 0 0 0 0 0 0 0 0 x x x x x x
0 0 0 0 0 0 0 0 0 x x x x x x
1 0 0 0 0 0 0 0 0 x x x x x x
0 0 0 0 0 0 0 0 0 x x x x x x
1 0 0 0 0 0 0 0 0 x x x x x x
0 0 0 0 0 0 0 0 0 x x x x x x
1 0 0 0 0 0 0 0 0 x x x x x x
0 0 0 0 0 0 0 0 0 0 0 0 0 0 0
1 0 0 0 0 0 0 0 0 0 0 0 0 0 0
0 0 0 0 1 0 0 0 0 0 0 0 0 0 0
1 0 0 0 1 0 0 0 0 0 0 0 0 0 0
0 0 0 0 0 0 0 0 0 x x x x x x
1 0 0 0 0 0 0 0 0 x x x x x x
0 0 0 0 0 0 0 0 0 x x x x x x
1 0 0 0 0 0 0 0 0 x x x x x x
0 0 0 0 0 0 0 0 0 x x x x x x
1 0 0 0 0 0 0 0 0 x x x x x x
0 0 0 0 0 0 0 0 0 x x x x x x
1 0 0 0 0 0 0 0 0 x x x x x x
0 0 0 0 0 0 0 0 0 x x x x x x
1 0 0 0 0 0 0 0 0 x x x x x x
0 0 0 0 0 0 0 0 0 x x x x x x
1 0 0 0 0 0 0 0 0 x x x x x x
0 0 0 0 0 0 0 0 0 x x x x x x
1 0 0 0 0 0 0 0 0 x x x x x x
0 0 0 0 0 0 0 0 0 x x x x x x
1 0 0 0 0 0 0 0 0 x x x x x x
0 0 0 0 0 0 0 0 0 x x x x x x
1 0 0 0 0 0 0 0 0 x x x x x x
0 0 0 0 0 0 0 0 0 x x x x x x
1 0 0 0 0 0 0 0 0 x x x x x x
0 0 0 0 0 0 0 0 0 x x x x x x
1 0 0 0 0 0 0 0 0 x x x x x x
0 0 0 0 0 0 0 0 0 x x x x x x
1 0 0 0 0 0 0 0 0 x x x x x x
0 0 0 0 0 0 0 0 0 x x x x x x
1 0 0 0 0 0 0 0 0 x x x x x x
0 0 0 0 0 0 0 0 0 x x x x x x
1 0 0 0 0 0 0 0 0 x x x x x x
0 0 0 0 0 0 0 0 0 x x x x x x
1 0 0 0 0 0 0 0 0 x x x x x x
0 0 0 0 0 0 0 0 0 x x x x x x
1 0 0 0 0 0 0 0 0 x x x x x x
0 0 0 0 0 0 0 0 0 x x x x x x
1 0 0 0 0 0 0 0 0 x x x x x x
0 0 0 0 0 0 0 0 0 x x x x x x
1 0 0 0 0 0 0 0 0 x x x x x x
0 0 0 0 0 0 0 0 0 x x x x x x
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*/

/* Test case T3:
clock reset P5 P10 P20 Pcoffee Ptea Pchange Pnext Balance CoffeeOut TeaOut Change5 Change10 Change20
0 1 0 0 0 0 0 0 0 x x x x x x
1 1 0 0 0 0 0 0 0 0 0 0 0 0 0
0 0 1 0 0 0 0 0 0 0 0 0 0 0 0
1 0 1 0 0 0 0 0 0 0 0 0 0 0 0
0 0 0 0 0 0 0 0 0 x x x x x x
1 0 0 0 0 0 0 0 0 x x x x x x
0 0 0 0 0 0 0 0 0 x x x x x x
1 0 0 0 0 0 0 0 0 x x x x x x
0 0 0 0 0 0 0 0 0 x x x x x x
1 0 0 0 0 0 0 0 0 x x x x x x
0 0 0 0 0 0 0 0 0 x x x x x x
1 0 0 0 0 0 0 0 0 x x x x x x
0 0 0 0 0 0 0 0 0 x x x x x x
1 0 0 0 0 0 0 0 0 x x x x x x
0 0 0 0 0 0 0 0 0 x x x x x x
1 0 0 0 0 0 0 0 0 x x x x x x
0 0 0 0 0 0 0 0 0 x x x x x x
1 0 0 0 0 0 0 0 0 x x x x x x
0 0 0 0 0 0 0 0 0 x x x x x x
1 0 0 0 0 0 0 0 0 x x x x x x
0 0 0 0 0 0 0 0 0 x x x x x x
1 0 0 0 0 0 0 0 0 x x x x x x
0 0 0 0 0 0 0 0 0 x x x x x x
1 0 0 0 0 0 0 0 0 x x x x x x
0 0 0 0 0 0 0 0 0 x x x x x x
1 0 0 0 0 0 0 0 0 x x x x x x
0 0 0 0 0 0 0 0 0 x x x x x x
1 0 0 0 0 0 0 0 0 x x x x x x
0 0 0 0 0 0 0 0 0 x x x x x x
1 0 0 0 0 0 0 0 0 x x x x x x
0 0 0 0 0 0 0 0 0 x x x x x x
1 0 0 0 0 0 0 0 0 x x x x x x
0 0 0 0 0 0 0 0 0 x x x x x x
1 0 0 0 0 0 0 0 0 x x x x x x
0 0 0 0 0 0 0 0 0 x x x x x x
1 0 0 0 0 0 0 0 0 x x x x x x
0 0 0 0 0 0 0 0 0 x x x x x x
1 0 0 0 0 0 0 0 0 x x x x x x
0 0 0 0 0 0 0 0 0 x x x x x x
1 0 0 0 0 0 0 0 0 x x x x x x
0 0 0 0 0 0 0 0 0 x x x x x x
1 0 0 0 0 0 0 0 0 x x x x x x
0 0 0 0 0 0 0 0 0 x x x x x x
1 0 0 0 0 0 0 0 0 x x x x x x
0 0 0 0 0 0 0 0 0 5 0 0 0 0 0
1 0 0 0 0 0 0 0 0 5 0 0 0 0 0
0 0 0 0 0 0 0 1 0 5 0 0 0 0 0
1 0 0 0 0 0 0 1 0 5 0 0 0 0 0
0 0 0 0 0 0 0 0 0 x x x x x x
1 0 0 0 0 0 0 0 0 x x x x x x
0 0 0 0 0 0 0 0 0 x x x x x x
1 0 0 0 0 0 0 0 0 x x x x x x
0 0 0 0 0 0 0 0 0 x x x x x x
1 0 0 0 0 0 0 0 0 x x x x x x
0 0 0 0 0 0 0 0 0 x x x x x x
1 0 0 0 0 0 0 0 0 x x x x x x
0 0 0 0 0 0 0 0 0 x x x x x x
1 0 0 0 0 0 0 0 0 x x x x x x
0 0 0 0 0 0 0 0 0 x x x x x x
1 0 0 0 0 0 0 0 0 x x x x x x
0 0 0 0 0 0 0 0 0 x x x x x x
1 0 0 0 0 0 0 0 0 x x x x x x
0 0 0 0 0 0 0 0 0 x x x x x x
1 0 0 0 0 0 0 0 0 x x x x x x
0 0 0 0 0 0 0 0 0 x x x x x x
1 0 0 0 0 0 0 0 0 x x x x x x
0 0 0 0 0 0 0 0 0 x x x x x x
1 0 0 0 0 0 0 0 0 x x x x x x
0 0 0 0 0 0 0 0 0 x x x x x x
1 0 0 0 0 0 0 0 0 x x x x x x
0 0 0 0 0 0 0 0 0 x x x x x x
1 0 0 0 0 0 0 0 0 x x x x x x
0 0 0 0 0 0 0 0 0 x x x x x x
1 0 0 0 0 0 0 0 0 x x x x x x
0 0 0 0 0 0 0 0 0 x x x x x x
1 0 0 0 0 0 0 0 0 x x x x x x
0 0 0 0 0 0 0 0 0 x x x x x x
1 0 0 0 0 0 0 0 0 x x x x x x
0 0 0 0 0 0 0 0 0 x x x x x x
1 0 0 0 0 0 0 0 0 x x x x x x
0 0 0 0 0 0 0 0 0 x x x x x x
1 0 0 0 0 0 0 0 0 x x x x x x
0 0 0 0 0 0 0 0 0 x x x x x x
1 0 0 0 0 0 0 0 0 x x x x x x
0 0 0 0 0 0 0 0 0 x x x x x x
1 0 0 0 0 0 0 0 0 x x x x x x
0 0 0 0 0 0 0 0 0 x x x x x x
1 0 0 0 0 0 0 0 0 x x x x x x
0 0 0 0 0 0 0 0 0 0 0 0 1 0 0
1 0 0 0 0 0 0 0 0 0 0 0 1 0 0
0 0 0 1 0 0 0 0 0 0 0 0 1 0 0
1 0 0 1 0 0 0 0 0 0 0 0 1 0 0
0 0 0 0 0 0 0 0 0 x x x x x x
1 0 0 0 0 0 0 0 0 x x x x x x
0 0 0 0 0 0 0 0 0 x x x x x x
1 0 0 0 0 0 0 0 0 x x x x x x
0 0 0 0 0 0 0 0 0 x x x x x x
1 0 0 0 0 0 0 0 0 x x x x x x
0 0 0 0 0 0 0 0 0 x x x x x x
1 0 0 0 0 0 0 0 0 x x x x x x
0 0 0 0 0 0 0 0 0 x x x x x x
1 0 0 0 0 0 0 0 0 x x x x x x
0 0 0 0 0 0 0 0 0 x x x x x x
1 0 0 0 0 0 0 0 0 x x x x x x
0 0 0 0 0 0 0 0 0 x x x x x x
1 0 0 0 0 0 0 0 0 x x x x x x
0 0 0 0 0 0 0 0 0 x x x x x x
1 0 0 0 0 0 0 0 0 x x x x x x
0 0 0 0 0 0 0 0 0 x x x x x x
1 0 0 0 0 0 0 0 0 x x x x x x
0 0 0 0 0 0 0 0 0 x x x x x x
1 0 0 0 0 0 0 0 0 x x x x x x
0 0 0 0 0 0 0 0 0 x x x x x x
1 0 0 0 0 0 0 0 0 x x x x x x
0 0 0 0 0 0 0 0 0 x x x x x x
1 0 0 0 0 0 0 0 0 x x x x x x
0 0 0 0 0 0 0 0 0 x x x x x x
1 0 0 0 0 0 0 0 0 x x x x x x
0 0 0 0 0 0 0 0 0 x x x x x x
1 0 0 0 0 0 0 0 0 x x x x x x
0 0 0 0 0 0 0 0 0 x x x x x x
1 0 0 0 0 0 0 0 0 x x x x x x
0 0 0 0 0 0 0 0 0 x x x x x x
1 0 0 0 0 0 0 0 0 x x x x x x
0 0 0 0 0 0 0 0 0 x x x x x x
1 0 0 0 0 0 0 0 0 x x x x x x
0 0 0 0 0 0 0 0 0 x x x x x x
1 0 0 0 0 0 0 0 0 x x x x x x
0 0 0 0 0 0 0 0 0 x x x x x x
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*/

/* Test case T4:
clock reset P5 P10 P20 Pcoffee Ptea Pchange Pnext Balance CoffeeOut TeaOut Change5 Change10 Change20
0 1 0 0 0 0 0 0 0 x x x x x x
1 1 0 0 0 0 0 0 0 0 0 0 0 0 0
0 0 0 0 1 0 0 0 0 0 0 0 0 0 0
1 0 0 0 1 0 0 0 0 0 0 0 0 0 0
0 0 0 0 0 0 0 0 0 x x x x x x
1 0 0 0 0 0 0 0 0 x x x x x x
0 0 0 0 0 0 0 0 0 x x x x x x
1 0 0 0 0 0 0 0 0 x x x x x x
0 0 0 0 0 0 0 0 0 x x x x x x
1 0 0 0 0 0 0 0 0 x x x x x x
0 0 0 0 0 0 0 0 0 x x x x x x
1 0 0 0 0 0 0 0 0 x x x x x x
0 0 0 0 0 0 0 0 0 x x x x x x
1 0 0 0 0 0 0 0 0 x x x x x x
0 0 0 0 0 0 0 0 0 x x x x x x
1 0 0 0 0 0 0 0 0 x x x x x x
0 0 0 0 0 0 0 0 0 x x x x x x
1 0 0 0 0 0 0 0 0 x x x x x x
0 0 0 0 0 0 0 0 0 x x x x x x
1 0 0 0 0 0 0 0 0 x x x x x x
0 0 0 0 0 0 0 0 0 x x x x x x
1 0 0 0 0 0 0 0 0 x x x x x x
0 0 0 0 0 0 0 0 0 x x x x x x
1 0 0 0 0 0 0 0 0 x x x x x x
0 0 0 0 0 0 0 0 0 x x x x x x
1 0 0 0 0 0 0 0 0 x x x x x x
0 0 0 0 0 0 0 0 0 x x x x x x
1 0 0 0 0 0 0 0 0 x x x x x x
0 0 0 0 0 0 0 0 0 x x x x x x
1 0 0 0 0 0 0 0 0 x x x x x x
0 0 0 0 0 0 0 0 0 x x x x x x
1 0 0 0 0 0 0 0 0 x x x x x x
0 0 0 0 0 0 0 0 0 x x x x x x
1 0 0 0 0 0 0 0 0 x x x x x x
0 0 0 0 0 0 0 0 0 x x x x x x
1 0 0 0 0 0 0 0 0 x x x x x x
0 0 0 0 0 0 0 0 0 x x x x x x
1 0 0 0 0 0 0 0 0 x x x x x x
0 0 0 0 0 0 0 0 0 x x x x x x
1 0 0 0 0 0 0 0 0 x x x x x x
0 0 0 0 0 0 0 0 0 x x x x x x
1 0 0 0 0 0 0 0 0 x x x x x x
0 0 0 0 0 0 0 0 0 x x x x x x
1 0 0 0 0 0 0 0 0 x x x x x x
0 0 0 0 0 0 0 0 0 20 0 0 0 0 0
1 0 0 0 0 0 0 0 0 20 0 0 0 0 0
0 0 0 0 1 0 0 0 0 20 0 0 0 0 0
1 0 0 0 1 0 0 0 0 20 0 0 0 0 0
0 0 0 0 0 0 0 0 0 x x x x x x
1 0 0 0 0 0 0 0 0 x x x x x x
0 0 0 0 0 0 0 0 0 x x x x x x
1 0 0 0 0 0 0 0 0 x x x x x x
0 0 0 0 0 0 0 0 0 x x x x x x
1 0 0 0 0 0 0 0 0 x x x x x x
0 0 0 0 0 0 0 0 0 x x x x x x
1 0 0 0 0 0 0 0 0 x x x x x x
0 0 0 0 0 0 0 0 0 x x x x x x
1 0 0 0 0 0 0 0 0 x x x x x x
0 0 0 0 0 0 0 0 0 x x x x x x
1 0 0 0 0 0 0 0 0 x x x x x x
0 0 0 0 0 0 0 0 0 x x x x x x
1 0 0 0 0 0 0 0 0 x x x x x x
0 0 0 0 0 0 0 0 0 x x x x x x
1 0 0 0 0 0 0 0 0 x x x x x x
0 0 0 0 0 0 0 0 0 x x x x x x
1 0 0 0 0 0 0 0 0 x x x x x x
0 0 0 0 0 0 0 0 0 x x x x x x
1 0 0 0 0 0 0 0 0 x x x x x x
0 0 0 0 0 0 0 0 0 x x x x x x
1 0 0 0 0 0 0 0 0 x x x x x x
0 0 0 0 0 0 0 0 0 x x x x x x
1 0 0 0 0 0 0 0 0 x x x x x x
0 0 0 0 0 0 0 0 0 x x x x x x
1 0 0 0 0 0 0 0 0 x x x x x x
0 0 0 0 0 0 0 0 0 x x x x x x
1 0 0 0 0 0 0 0 0 x x x x x x
0 0 0 0 0 0 0 0 0 x x x x x x
1 0 0 0 0 0 0 0 0 x x x x x x
0 0 0 0 0 0 0 0 0 x x x x x x
1 0 0 0 0 0 0 0 0 x x x x x x
0 0 0 0 0 0 0 0 0 x x x x x x
1 0 0 0 0 0 0 0 0 x x x x x x
0 0 0 0 0 0 0 0 0 x x x x x x
1 0 0 0 0 0 0 0 0 x x x x x x
0 0 0 0 0 0 0 0 0 x x x x x x
1 0 0 0 0 0 0 0 0 x x x x x x
0 0 0 0 0 0 0 0 0 x x x x x x
1 0 0 0 0 0 0 0 0 x x x x x x
0 0 0 0 0 0 0 0 0 40 0 0 0 0 0
1 0 0 0 0 0 0 0 0 40 0 0 0 0 0
0 0 0 0 0 0 1 0 0 40 0 0 0 0 0
1 0 0 0 0 0 1 0 0 40 0 0 0 0 0
0 0 0 0 0 0 0 0 0 x x x x x x
1 0 0 0 0 0 0 0 0 x x x x x x
0 0 0 0 0 0 0 0 0 x x x x x x
1 0 0 0 0 0 0 0 0 x x x x x x
0 0 0 0 0 0 0 0 0 x x x x x x
1 0 0 0 0 0 0 0 0 x x x x x x
0 0 0 0 0 0 0 0 0 x x x x x x
1 0 0 0 0 0 0 0 0 x x x x x x
0 0 0 0 0 0 0 0 0 x x x x x x
1 0 0 0 0 0 0 0 0 x x x x x x
0 0 0 0 0 0 0 0 0 x x x x x x
1 0 0 0 0 0 0 0 0 x x x x x x
0 0 0 0 0 0 0 0 0 x x x x x x
1 0 0 0 0 0 0 0 0 x x x x x x
0 0 0 0 0 0 0 0 0 x x x x x x
1 0 0 0 0 0 0 0 0 x x x x x x
0 0 0 0 0 0 0 0 0 x x x x x x
1 0 0 0 0 0 0 0 0 x x x x x x
0 0 0 0 0 0 0 0 0 x x x x x x
1 0 0 0 0 0 0 0 0 x x x x x x
0 0 0 0 0 0 0 0 0 x x x x x x
1 0 0 0 0 0 0 0 0 x x x x x x
0 0 0 0 0 0 0 0 0 x x x x x x
1 0 0 0 0 0 0 0 0 x x x x x x
0 0 0 0 0 0 0 0 0 x x x x x x
1 0 0 0 0 0 0 0 0 x x x x x x
0 0 0 0 0 0 0 0 0 x x x x x x
1 0 0 0 0 0 0 0 0 x x x x x x
0 0 0 0 0 0 0 0 0 x x x x x x
1 0 0 0 0 0 0 0 0 x x x x x x
0 0 0 0 0 0 0 0 0 x x x x x x
1 0 0 0 0 0 0 0 0 x x x x x x
0 0 0 0 0 0 0 0 0 x x x x x x
1 0 0 0 0 0 0 0 0 x x x x x x
0 0 0 0 0 0 0 0 0 x x x x x x
1 0 0 0 0 0 0 0 0 x x x x x x
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*/
