// Digital circuit 01.dig as structural Verilog
module _01 (
  input  [2:0] B,
  input  [2:0] A,
  output Output
);

  wire and_1_out, and_2_out, and_3_out, and_5_out, and_6_out, and_7_out, C1, C2, not_1_out, not_2_out,
       not_3_out, S0, S1, S2, S3, xor_1_out, xor_2_out, xor_4_out, xor_5_out;

  or or_1 (C2, and_3_out, and_5_out);
  or or_2 (S3, and_2_out, and_6_out, and_1_out);
  and and_1 (and_1_out, xor_2_out, xor_1_out, C1);
  and and_2 (and_2_out, xor_2_out, and_5_out);
  and and_3 (and_3_out, xor_1_out, C1);
  and and_4 (C1, B[0], A[0]);
  and and_5 (and_5_out, B[1], A[1]);
  xor xor_1 (xor_1_out, B[1], A[1]);
  and and_6 (and_6_out, B[2], A[2]);
  xor xor_2 (xor_2_out, B[2], A[2]);
  xor xor_3 (S0, A[0], B[0]);
  xor xor_4 (xor_4_out, A[1], B[1]);
  xor xor_5 (xor_5_out, A[2], B[2]);
  xor xor_6 (S1, xor_4_out, C1);
  xor xor_7 (S2, xor_5_out, C2);
  not not_1 (not_1_out, S1);
  not not_2 (not_2_out, S2);
  not not_3 (not_3_out, S3);
  and and_7 (and_7_out, not_1_out, not_2_out);
  or or_3 (Output, and_7_out, not_3_out);
  Seven_Seg seven_seg_1 (.a(Output), .b(1'b1), .c(1'b1), .d(Output), .e(Output), .f(Output), .g(1'b0), .dp(1'b0));

  // Other names for the same wires on the sheet: a_t = Output

  // Notes on the sheet:
  //   G0
  //   G1
  //   P1
  //   G2
  //   P2
endmodule

/* Test case:
A B Output
0 0 1
0 1 1
0 2 1
0 3 1
0 4 1
0 5 1
0 6 1
0 7 1
1 0 1
1 1 1
1 2 1
1 3 1
1 4 1
1 5 1
1 6 1
1 7 1
2 0 1
2 1 1
2 2 1
2 3 1
2 4 1
2 5 1
2 6 1
2 7 1
3 0 1
3 1 1
3 2 1
3 3 1
3 4 1
3 5 1
3 6 1
3 7 0
4 0 1
4 1 1
4 2 1
4 3 1
4 4 1
4 5 1
4 6 0
4 7 0
5 0 1
5 1 1
5 2 1
5 3 1
5 4 1
5 5 0
5 6 0
5 7 0
6 0 1
6 1 1
6 2 1
6 3 1
6 4 0
6 5 0
6 6 0
6 7 0
7 0 1
7 1 1
7 2 1
7 3 0
7 4 0
7 5 0
7 6 0
7 7 0
*/
