// Digital circuit 02.dig as structural Verilog
module _02 (
  input  [2:0] S,
  output O1,
  output O2
);

  wire decoder_1_out_0, decoder_1_out_2, decoder_1_out_4, decoder_1_out_5, decoder_1_out_6, decoder_1_out_7;

  Decoder #(.Selector_Bits(3)) decoder_1 (
    .sel(S), .out_0(decoder_1_out_0), .out_2(decoder_1_out_2), .out_4(decoder_1_out_4),
    .out_5(decoder_1_out_5), .out_6(decoder_1_out_6), .out_7(decoder_1_out_7));  // open: out_1, out_3
  or or_1 (O1, decoder_1_out_6, decoder_1_out_5, decoder_1_out_4, decoder_1_out_2);
  or or_2 (O2, decoder_1_out_7, decoder_1_out_6, decoder_1_out_4, decoder_1_out_2, decoder_1_out_0);
endmodule

/* Test case:
S O1 O2
0 0 1
1 0 0
2 1 1
3 0 0
4 1 1
5 1 0
6 1 1
7 0 1
*/
